// Logisim project projet_G055.circ as structural Verilog: 56 circuits, main circuit main
module main (
  input  signal_A,
  input  signal_B,
  input  CH_C,
  output pwr,
  output gnd,
  output buzzer
);

  wire alarme, and_3_out, arret_horloge, ch_c_horloge, ch_c_menu, clk_bouton, clk_encodeur, clk_horloge,
       clk_minuit, clock_jeu_out, clock_message_out, clock_musique_jeu_out, counter_message, dip_switch_4,
       dip_switch_5, dip_switch_6, dip_switch_7, dip_switch_8, dip_switch_9, dip_switch_10, enable_counter,
       f_do_bas_out, f_do_out, f_fa_diese_out, f_fa_out, f_la_out, f_mi_out, f_re_haut_out, f_re_out,
       f_si_out, f_sol_out, fonction_complexe, fonction_enable, horloge_1_minuit, mode_heure_fonction,
       mode_heure_horloge, mode_min_fonction, mode_min_horloge, mode_sec_fonction, mode_sec_horloge,
       mode_set, not_1_out, not_2_out, or_1_out, or_2_out, or_4_out, or_5_out, or_6_out, or_7_out,
       reset_asynchrone, reset_general, retour_horloge, set_heure, set_menu_1_mode_abc, set_song,
       start_chrono, start_jeu, start_stop;
  wire [1:0] counter_3_q, enable_message, enable_musique;
  wire [2:0] set_menu_1_fonctions_on;
  wire [3:0] multiplexer_1_out, multiplexer_2_out, multiplexer_3_out, multiplexer_4_out, multiplexer_5_out,
       multiplexer_6_out;
  wire [6:0] set_menu_1_led, set_menu_1_letter_1, set_menu_1_letter_2, set_menu_1_letter_3,
       set_menu_1_letter_4, set_menu_1_letter_5, set_menu_1_letter_6;
  wire [7:0] heure_fonction, heure_reel, minute_fonction, minute_reel, seconde_fonction, seconde_reel;

  DipSwitch #(.number(10)) DipSwitch_1 (
    .sw1(mode_set), .sw2(alarme), .sw3(reset_general), .sw4(dip_switch_4), .sw5(dip_switch_5),
    .sw6(dip_switch_6), .sw7(dip_switch_7), .sw8(dip_switch_8), .sw9(dip_switch_9), .sw10(dip_switch_10));
  Button u_reset_asynchrone (.out(reset_asynchrone));
  Button u_start_chrono (.out(start_stop));
  Clock #(.highDuration(102), .lowDuration(102)) f_re (.out(f_re_out));
  Clock #(.highDuration(91), .lowDuration(91)) f_mi (.out(f_mi_out));
  Clock #(.highDuration(81), .lowDuration(81)) f_fa_diese (.out(f_fa_diese_out));
  Clock #(.highDuration(77), .lowDuration(77)) f_sol (.out(f_sol_out));
  Clock #(.highDuration(68), .lowDuration(68)) f_la (.out(f_la_out));
  Clock #(.highDuration(61), .lowDuration(61)) f_si (.out(f_si_out));
  Clock #(.highDuration(57), .lowDuration(57)) f_do (.out(f_do_out));
  Clock #(.highDuration(51), .lowDuration(51)) f_re_haut (.out(f_re_haut_out));
  Clock #(.highDuration(115), .lowDuration(115)) f_do_bas (.out(f_do_bas_out));
  Clock #(.highDuration(86), .lowDuration(86)) f_fa (.out(f_fa_out));
  Clock #(.highDuration(10000), .lowDuration(10000)) clock_message (.out(clock_message_out));
  Clock #(.highDuration(5000), .lowDuration(5000)) clock_musique_jeu (.out(clock_musique_jeu_out));
  Clock #(.highDuration(7500), .lowDuration(7500)) clock_jeu (.out(clock_jeu_out));
  and and_1 (ch_c_horloge, mode_set, ~CH_C);  // AND_Gate
  and and_2 (ch_c_menu, ~CH_C, ~mode_set);  // AND_Gate
  horloge horloge_1 (
    .Clk_bouton(clk_bouton), .Clk_horloge(clk_horloge), .Mode_set(mode_set), .Encodeur({signal_B, signal_A}),
    .Reset(reset_general), .CH_C(ch_c_horloge), .Set_heure(set_heure), .Clk_encodeur(clk_encodeur),
    .Clk_minuit(clk_minuit), .retour_horloge(retour_horloge), .Mode_sec(mode_sec_horloge),
    .Mode_min(mode_min_horloge), .Mode_heure(mode_heure_horloge), .Secondes(seconde_reel),
    .Minutes(minute_reel), .Heures(heure_reel), .Minuit(horloge_1_minuit));
  Clock #(.highDuration(30000), .lowDuration(30000)) clock_heure (.out(clk_horloge));
  Clock #(.highDuration(3750), .lowDuration(3750)) clock_bouton (.out(clk_bouton));
  Clock clock_encodeur (.out(clk_encodeur));
  Clock #(.highDuration(29999), .lowDuration(29999)) clock_minuit (.out(clk_minuit));
  Demultiplexer #(.enable("true"), .select(3)) demultiplexer_1 (
    .out0(enable_counter), .out1(set_heure), .out2(start_jeu), .out6(counter_message), .in(start_stop),
    .sel({set_song, fonction_complexe, mode_set}), .en(1'b1));  // open: out3, out4, out5, out7
  set_menu set_menu_1 (
    .Clock(clk_horloge), .Clock_bouton(clk_bouton), .CH_C(ch_c_menu), .Encodeur({signal_B, signal_A}),
    .Start_chrono(start_chrono), .Alarme_on(alarme), .Reset(reset_general), .Secondes_reel(seconde_reel),
    .Minutes_reel(minute_reel), .Heures_reel(heure_reel), .Reset_chrono(reset_asynchrone),
    .Input_1(dip_switch_4), .Input_2(dip_switch_5), .Input_3(dip_switch_6), .Input_4(dip_switch_7),
    .Input_5(dip_switch_8), .Input_6(dip_switch_9), .Input_7(dip_switch_10),
    .Start_fonction_complexe(start_jeu), .Re(f_re_out), .Mi(f_mi_out), .Fa_diese(f_fa_diese_out),
    .Sol(f_sol_out), .La(f_la_out), .Si(f_si_out), .Do(f_do_out), .Re_haut(f_re_haut_out),
    .Do_bas(f_do_bas_out), .Fa(f_fa_out), .Clock_message(clock_message_out),
    .Clock_musique(clock_musique_jeu_out), .Clock_jeu(clock_jeu_out), .Clk_encodeur(clk_encodeur),
    .Enable_message(enable_message), .Enable_musique(enable_musique), .Secondes(seconde_fonction),
    .Minutes(minute_fonction), .Heures(heure_fonction), .Buzzer(buzzer), .Mode_abc(set_menu_1_mode_abc),
    .Fonctions_on(set_menu_1_fonctions_on), .Fonction_complexe(fonction_complexe), .LED(set_menu_1_led),
    .Letter_1(set_menu_1_letter_1), .Letter_2(set_menu_1_letter_2), .Letter_3(set_menu_1_letter_3),
    .Letter_4(set_menu_1_letter_4), .Letter_5(set_menu_1_letter_5), .Letter_6(set_menu_1_letter_6),
    .Set_song(set_song), .Mode_sec(mode_sec_fonction), .Mode_min(mode_min_fonction),
    .Mode_heure(mode_heure_fonction), .Fonction_enable(fonction_enable));
  or or_1 (or_1_out, set_menu_1_mode_abc, set_menu_1_fonctions_on[0], set_menu_1_fonctions_on[1], set_menu_1_fonctions_on[2]);
  Counter #(.max('h3), .width(2)) counter_1 (
    .clr(reset_general), .load(not_1_out), .up(1'b1), .count(and_3_out), .clk(clk_bouton), .D(2'b00),
    .Q(enable_musique));  // open: carry
  not not_1 (not_1_out, set_song);
  and and_3 (and_3_out, set_song, reset_asynchrone);
  Counter #(.max('h3), .width(2)) counter_2 (
    .clr(reset_general), .load(not_2_out), .up(1'b1), .count(counter_message), .clk(clk_bouton), .D(2'b00),
    .Q(enable_message));  // open: carry
  not not_2 (not_2_out, set_song);
  Counter #(.max('h1), .width(2)) counter_3 (
    .clr(reset_general), .load(or_2_out), .up(1'b1), .count(enable_counter), .clk(clk_bouton), .D(2'b00),
    .Q(counter_3_q));  // open: carry
  or or_2 (or_2_out, reset_asynchrone, set_menu_1_mode_abc);
  and and_4 (arret_horloge, or_1_out, ~mode_set);  // AND_Gate
  or or_3 (start_chrono, counter_3_q[0], counter_3_q[1]);
  LED LED_4 (.in(set_menu_1_led[0]));
  LED LED_5 (.in(set_menu_1_led[1]));
  LED LED_6 (.in(set_menu_1_led[2]));
  LED LED_7 (.in(set_menu_1_led[3]));
  LED LED_8 (.in(set_menu_1_led[4]));
  LED LED_9 (.in(set_menu_1_led[5]));
  LED LED_10 (.in(set_menu_1_led[6]));
  or or_4 (or_4_out, mode_heure_horloge, horloge_1_minuit, or_7_out, mode_heure_fonction);
  or or_5 (or_5_out, mode_min_horloge, or_7_out, mode_min_fonction);
  or or_6 (or_6_out, mode_sec_horloge, or_7_out, mode_sec_fonction);
  or or_7 (or_7_out, fonction_enable, retour_horloge);
  LED LED_1 (.in(or_4_out));
  LED LED_2 (.in(or_5_out));
  LED LED_3 (.in(or_6_out));
  Multiplexer #(.width(4)) multiplexer_1 (
    .in0(seconde_reel[3:0]), .in1(seconde_fonction[3:0]), .out(multiplexer_1_out), .sel(arret_horloge));
  Multiplexer #(.width(4)) multiplexer_2 (
    .in0(seconde_reel[7:4]), .in1(seconde_fonction[7:4]), .out(multiplexer_2_out), .sel(arret_horloge));
  Multiplexer #(.width(4)) multiplexer_3 (
    .in0(minute_reel[3:0]), .in1(minute_fonction[3:0]), .out(multiplexer_3_out), .sel(arret_horloge));
  Multiplexer #(.width(4)) multiplexer_4 (
    .in0(minute_reel[7:4]), .in1(minute_fonction[7:4]), .out(multiplexer_4_out), .sel(arret_horloge));
  Multiplexer #(.width(4)) multiplexer_5 (
    .in0(heure_reel[3:0]), .in1(heure_fonction[3:0]), .out(multiplexer_5_out), .sel(arret_horloge));
  Multiplexer #(.width(4)) multiplexer_6 (
    .in0(heure_reel[7:4]), .in1(heure_fonction[7:4]), .out(multiplexer_6_out), .sel(arret_horloge));
  number_clock number_clock_1 (
    .letter(set_menu_1_letter_6), .function_complexe(fonction_complexe), .nbr(multiplexer_6_out));
  number_clock number_clock_2 (
    .letter(set_menu_1_letter_5), .function_complexe(fonction_complexe), .nbr(multiplexer_5_out));
  number_clock number_clock_3 (
    .letter(set_menu_1_letter_4), .function_complexe(fonction_complexe), .nbr(multiplexer_4_out));
  number_clock number_clock_4 (
    .letter(set_menu_1_letter_3), .function_complexe(fonction_complexe), .nbr(multiplexer_3_out));
  number_clock number_clock_5 (
    .letter(set_menu_1_letter_2), .function_complexe(fonction_complexe), .nbr(multiplexer_2_out));
  number_clock number_clock_6 (
    .letter(set_menu_1_letter_1), .function_complexe(fonction_complexe), .nbr(multiplexer_1_out));

  assign gnd = 1'b0;
  assign pwr = 1'b1;

  // Other names for the same wires on the sheet: encodeur[1:0] = {signal_B, signal_A}

  // Notes on the sheet:
  //   1 choose, 2 return to menu, 3 return to horloge
endmodule

module horloge (
  input  Clk_bouton,
  input  Clk_horloge,
  input  Mode_set,
  input  [1:0] Encodeur,
  input  Reset,
  input  CH_C,
  input  Set_heure,
  input  Clk_encodeur,
  input  Clk_minuit,
  output retour_horloge,
  output Mode_sec,
  output Mode_min,
  output Mode_heure,
  output [7:0] Secondes,
  output [7:0] Minutes,
  output [7:0] Heures,
  output Minuit
);

  wire and_2_out, and_3_out, and_4_out, and_5_out, and_6_out, and_7_out, and_8_out, and_9_out, and_10_out,
       and_11_out, and_12_out, and_13_out, and_14_out, and_15_out, and_16_out, and_17_out, and_18_out,
       and_19_out, and_20_out, and_21_out, and_22_out, and_23_out, and_24_out, and_25_out, and_26_out,
       and_27_out, and_28_out, and_29_out, and_30_out, and_31_out, and_32_out, and_33_out, and_34_out,
       and_35_out, and_36_out, and_37_out, and_38_out, and_39_out, and_40_out, and_41_out, and_42_out,
       and_43_out, and_44_out, and_45_out, and_46_out, and_47_out, and_48_out, and_49_out, and_50_out,
       d_ff_1_q, d_ff_2_q, incrementeur_1_1_carry_out, incrementeur_1_1_output_1, incrementeur_1_1_output_2,
       incrementeur_1_1_output_3, incrementeur_1_1_output_4, incrementeur_horloge_1_carry_out,
       incrementeur_horloge_1_p0, incrementeur_horloge_1_p1, incrementeur_horloge_1_p2,
       incrementeur_horloge_1_p3, incrementeur_horloge_heure1_1_carry_out, incrementeur_horloge_heure1_1_p0,
       incrementeur_horloge_heure1_1_p1, incrementeur_horloge_heure1_1_p2, incrementeur_horloge_heure1_1_p3,
       incrementeur_horloge_heure1_1_reset, incrementeur_horloge_heure2_1_if_2,
       incrementeur_horloge_heure2_1_p0, incrementeur_horloge_heure2_1_p1, incrementeur_horloge_heure2_1_p2,
       incrementeur_horloge_heure2_1_p3, incrementeur_horloge_min1_1_carry_out,
       incrementeur_horloge_min1_1_p0, incrementeur_horloge_min1_1_p1, incrementeur_horloge_min1_1_p2,
       incrementeur_horloge_min1_1_p3, incrementeur_horloge_min1_2_carry_out, incrementeur_horloge_min1_2_p0,
       incrementeur_horloge_min1_2_p1, incrementeur_horloge_min1_2_p2, incrementeur_horloge_min1_2_p3,
       mult_chiffre_1_output_mult, mult_chiffre_1_output_reel, mult_chiffre_2_output_mult,
       mult_chiffre_2_output_reel, mult_chiffre_3_output_mult, mult_chiffre_3_output_reel,
       mult_chiffre_4_output_mult, mult_chiffre_4_output_reel, mult_chiffre_5_output_mult,
       mult_chiffre_5_output_reel, mult_chiffre_6_output_mult, mult_chiffre_6_output_reel,
       mult_chiffre_7_output_mult, mult_chiffre_7_output_reel, mult_chiffre_8_output_mult,
       mult_chiffre_8_output_reel, mult_chiffre_9_output_mult, mult_chiffre_9_output_reel,
       mult_chiffre_10_output_mult, mult_chiffre_10_output_reel, mult_chiffre_11_output_mult,
       mult_chiffre_11_output_reel, mult_chiffre_12_output_mult, mult_chiffre_12_output_reel,
       mult_chiffre_13_output_mult, mult_chiffre_13_output_reel, mult_chiffre_14_output_mult,
       mult_chiffre_14_output_reel, mult_chiffre_15_output_mult, mult_chiffre_15_output_reel,
       mult_chiffre_16_output_mult, mult_chiffre_16_output_reel, mult_chiffre_17_output_mult,
       mult_chiffre_17_output_reel, mult_chiffre_18_output_mult, mult_chiffre_18_output_reel,
       mult_chiffre_19_output_mult, mult_chiffre_19_output_reel, mult_chiffre_20_output_mult,
       mult_chiffre_20_output_reel, mult_chiffre_21_output_mult, mult_chiffre_21_output_reel,
       mult_chiffre_22_output_mult, mult_chiffre_22_output_reel, mult_chiffre_23_output_mult,
       mult_chiffre_23_output_reel, mult_chiffre_24_output_mult, mult_chiffre_24_output_reel;
  wire [7:0] set_horloge_1_heures, set_horloge_1_minutes, set_horloge_1_secondes;

  and and_1 (Minuit, incrementeur_horloge_heure1_1_reset, incrementeur_horloge_heure1_1_carry_out, incrementeur_horloge_min1_2_carry_out, incrementeur_horloge_1_carry_out, incrementeur_horloge_min1_1_carry_out, incrementeur_1_1_carry_out);
  incrementeur_1 incrementeur_1_1 (
    .Input_1(mult_chiffre_1_output_reel), .Input_2(mult_chiffre_2_output_reel),
    .Input_3(mult_chiffre_3_output_reel), .Input_4(mult_chiffre_4_output_reel),
    .Output_1(incrementeur_1_1_output_1), .Output_2(incrementeur_1_1_output_2),
    .Output_3(incrementeur_1_1_output_3), .Output_4(incrementeur_1_1_output_4),
    .Carry_out(incrementeur_1_1_carry_out));
  incrementeur_horloge_min1 incrementeur_horloge_min1_1 (
    .Y0(mult_chiffre_5_output_reel), .Y1(mult_chiffre_6_output_reel), .Y2(mult_chiffre_7_output_reel),
    .Y3(mult_chiffre_8_output_reel), .Carry_in(incrementeur_1_1_carry_out),
    .P0(incrementeur_horloge_min1_1_p0), .P1(incrementeur_horloge_min1_1_p1),
    .P2(incrementeur_horloge_min1_1_p2), .P3(incrementeur_horloge_min1_1_p3),
    .Carry_out(incrementeur_horloge_min1_1_carry_out));
  incrementeur_horloge incrementeur_horloge_1 (
    .Y0(mult_chiffre_9_output_reel), .Y1(mult_chiffre_10_output_reel), .Y2(mult_chiffre_11_output_reel),
    .Y3(mult_chiffre_12_output_reel), .Carry_in(incrementeur_horloge_min1_1_carry_out),
    .P0(incrementeur_horloge_1_p0), .P1(incrementeur_horloge_1_p1), .P2(incrementeur_horloge_1_p2),
    .P3(incrementeur_horloge_1_p3), .Carry_out(incrementeur_horloge_1_carry_out));
  incrementeur_horloge_min1 incrementeur_horloge_min1_2 (
    .Y0(mult_chiffre_13_output_reel), .Y1(mult_chiffre_14_output_reel), .Y2(mult_chiffre_15_output_reel),
    .Y3(mult_chiffre_16_output_reel), .Carry_in(incrementeur_horloge_1_carry_out),
    .P0(incrementeur_horloge_min1_2_p0), .P1(incrementeur_horloge_min1_2_p1),
    .P2(incrementeur_horloge_min1_2_p2), .P3(incrementeur_horloge_min1_2_p3),
    .Carry_out(incrementeur_horloge_min1_2_carry_out));
  incrementeur_horloge_heure1 incrementeur_horloge_heure1_1 (
    .Y0(mult_chiffre_17_output_reel), .Y1(mult_chiffre_18_output_reel), .Y2(mult_chiffre_19_output_reel),
    .Y3(mult_chiffre_20_output_reel), .Carry_in(incrementeur_horloge_min1_2_carry_out), .If_2(d_ff_1_q),
    .P0(incrementeur_horloge_heure1_1_p0), .P1(incrementeur_horloge_heure1_1_p1),
    .P2(incrementeur_horloge_heure1_1_p2), .P3(incrementeur_horloge_heure1_1_p3),
    .Carry_out(incrementeur_horloge_heure1_1_carry_out), .Reset(incrementeur_horloge_heure1_1_reset));
  incrementeur_horloge_heure2 incrementeur_horloge_heure2_1 (
    .Y0(mult_chiffre_21_output_reel), .Y1(mult_chiffre_22_output_reel), .Y2(mult_chiffre_23_output_reel),
    .Y3(mult_chiffre_24_output_reel), .Carry_in(incrementeur_horloge_heure1_1_carry_out),
    .P0(incrementeur_horloge_heure2_1_p0), .P1(incrementeur_horloge_heure2_1_p1),
    .P2(incrementeur_horloge_heure2_1_p2), .P3(incrementeur_horloge_heure2_1_p3),
    .if_2(incrementeur_horloge_heure2_1_if_2));  // open: Carry_out
  D_Flip_Flop d_ff_1 (
    .D(incrementeur_horloge_heure2_1_if_2), .clk(Clk_horloge), .Q(d_ff_1_q), .preset(1'b0), .reset(Reset));  // open: Qn
  D_Flip_Flop d_ff_2 (
    .D(incrementeur_horloge_heure1_1_reset), .clk(Clk_minuit), .Q(d_ff_2_q), .preset(Reset), .reset(1'b0));  // open: Qn
  mult_chiffre mult_chiffre_5 (
    .Output_mult(mult_chiffre_5_output_mult), .Output_reel(mult_chiffre_5_output_reel),
    .Input_mult(incrementeur_horloge_min1_1_p0), .Reset(d_ff_2_q), .Clock_mult(Clk_horloge),
    .Clock_set(Set_heure), .Set_value(set_horloge_1_secondes[4]), .Set_enable(and_50_out));
  mult_chiffre mult_chiffre_6 (
    .Output_mult(mult_chiffre_6_output_mult), .Output_reel(mult_chiffre_6_output_reel),
    .Input_mult(incrementeur_horloge_min1_1_p1), .Reset(d_ff_2_q), .Clock_mult(Clk_horloge),
    .Clock_set(Set_heure), .Set_value(set_horloge_1_secondes[5]), .Set_enable(and_50_out));
  mult_chiffre mult_chiffre_7 (
    .Output_mult(mult_chiffre_7_output_mult), .Output_reel(mult_chiffre_7_output_reel),
    .Input_mult(incrementeur_horloge_min1_1_p2), .Reset(d_ff_2_q), .Clock_mult(Clk_horloge),
    .Clock_set(Set_heure), .Set_value(set_horloge_1_secondes[6]), .Set_enable(and_50_out));
  mult_chiffre mult_chiffre_8 (
    .Output_mult(mult_chiffre_8_output_mult), .Output_reel(mult_chiffre_8_output_reel),
    .Input_mult(incrementeur_horloge_min1_1_p3), .Reset(d_ff_2_q), .Clock_mult(Clk_horloge),
    .Clock_set(Set_heure), .Set_value(set_horloge_1_secondes[7]), .Set_enable(and_50_out));
  mult_chiffre mult_chiffre_9 (
    .Output_mult(mult_chiffre_9_output_mult), .Output_reel(mult_chiffre_9_output_reel),
    .Input_mult(incrementeur_horloge_1_p0), .Reset(d_ff_2_q), .Clock_mult(Clk_horloge),
    .Clock_set(Set_heure), .Set_value(set_horloge_1_minutes[0]), .Set_enable(and_50_out));
  mult_chiffre mult_chiffre_10 (
    .Output_mult(mult_chiffre_10_output_mult), .Output_reel(mult_chiffre_10_output_reel),
    .Input_mult(incrementeur_horloge_1_p1), .Reset(d_ff_2_q), .Clock_mult(Clk_horloge),
    .Clock_set(Set_heure), .Set_value(set_horloge_1_minutes[1]), .Set_enable(and_50_out));
  mult_chiffre mult_chiffre_11 (
    .Output_mult(mult_chiffre_11_output_mult), .Output_reel(mult_chiffre_11_output_reel),
    .Input_mult(incrementeur_horloge_1_p2), .Reset(d_ff_2_q), .Clock_mult(Clk_horloge),
    .Clock_set(Set_heure), .Set_value(set_horloge_1_minutes[2]), .Set_enable(and_50_out));
  mult_chiffre mult_chiffre_12 (
    .Output_mult(mult_chiffre_12_output_mult), .Output_reel(mult_chiffre_12_output_reel),
    .Input_mult(incrementeur_horloge_1_p3), .Reset(d_ff_2_q), .Clock_mult(Clk_horloge),
    .Clock_set(Set_heure), .Set_value(set_horloge_1_minutes[3]), .Set_enable(and_50_out));
  mult_chiffre mult_chiffre_13 (
    .Output_mult(mult_chiffre_13_output_mult), .Output_reel(mult_chiffre_13_output_reel),
    .Input_mult(incrementeur_horloge_min1_2_p0), .Reset(d_ff_2_q), .Clock_mult(Clk_horloge),
    .Clock_set(Set_heure), .Set_value(set_horloge_1_minutes[4]), .Set_enable(and_50_out));
  mult_chiffre mult_chiffre_14 (
    .Output_mult(mult_chiffre_14_output_mult), .Output_reel(mult_chiffre_14_output_reel),
    .Input_mult(incrementeur_horloge_min1_2_p1), .Reset(d_ff_2_q), .Clock_mult(Clk_horloge),
    .Clock_set(Set_heure), .Set_value(set_horloge_1_minutes[5]), .Set_enable(and_50_out));
  mult_chiffre mult_chiffre_15 (
    .Output_mult(mult_chiffre_15_output_mult), .Output_reel(mult_chiffre_15_output_reel),
    .Input_mult(incrementeur_horloge_min1_2_p2), .Reset(d_ff_2_q), .Clock_mult(Clk_horloge),
    .Clock_set(Set_heure), .Set_value(set_horloge_1_minutes[6]), .Set_enable(and_50_out));
  mult_chiffre mult_chiffre_16 (
    .Output_mult(mult_chiffre_16_output_mult), .Output_reel(mult_chiffre_16_output_reel),
    .Input_mult(incrementeur_horloge_min1_2_p3), .Reset(d_ff_2_q), .Clock_mult(Clk_horloge),
    .Clock_set(Set_heure), .Set_value(set_horloge_1_minutes[7]), .Set_enable(and_50_out));
  mult_chiffre mult_chiffre_17 (
    .Output_mult(mult_chiffre_17_output_mult), .Output_reel(mult_chiffre_17_output_reel),
    .Input_mult(incrementeur_horloge_heure1_1_p0), .Reset(d_ff_2_q), .Clock_mult(Clk_horloge),
    .Clock_set(Set_heure), .Set_value(set_horloge_1_heures[0]), .Set_enable(and_50_out));
  mult_chiffre mult_chiffre_18 (
    .Output_mult(mult_chiffre_18_output_mult), .Output_reel(mult_chiffre_18_output_reel),
    .Input_mult(incrementeur_horloge_heure1_1_p1), .Reset(d_ff_2_q), .Clock_mult(Clk_horloge),
    .Clock_set(Set_heure), .Set_value(set_horloge_1_heures[1]), .Set_enable(and_50_out));
  mult_chiffre mult_chiffre_19 (
    .Output_mult(mult_chiffre_19_output_mult), .Output_reel(mult_chiffre_19_output_reel),
    .Input_mult(incrementeur_horloge_heure1_1_p2), .Reset(d_ff_2_q), .Clock_mult(Clk_horloge),
    .Clock_set(Set_heure), .Set_value(set_horloge_1_heures[2]), .Set_enable(and_50_out));
  mult_chiffre mult_chiffre_20 (
    .Output_mult(mult_chiffre_20_output_mult), .Output_reel(mult_chiffre_20_output_reel),
    .Input_mult(incrementeur_horloge_heure1_1_p3), .Reset(d_ff_2_q), .Clock_mult(Clk_horloge),
    .Clock_set(Set_heure), .Set_value(set_horloge_1_heures[3]), .Set_enable(and_50_out));
  mult_chiffre mult_chiffre_21 (
    .Output_mult(mult_chiffre_21_output_mult), .Output_reel(mult_chiffre_21_output_reel),
    .Input_mult(incrementeur_horloge_heure2_1_p0), .Reset(d_ff_2_q), .Clock_mult(Clk_horloge),
    .Clock_set(Set_heure), .Set_value(set_horloge_1_heures[4]), .Set_enable(and_50_out));
  mult_chiffre mult_chiffre_22 (
    .Output_mult(mult_chiffre_22_output_mult), .Output_reel(mult_chiffre_22_output_reel),
    .Input_mult(incrementeur_horloge_heure2_1_p1), .Reset(d_ff_2_q), .Clock_mult(Clk_horloge),
    .Clock_set(Set_heure), .Set_value(set_horloge_1_heures[5]), .Set_enable(and_50_out));
  mult_chiffre mult_chiffre_23 (
    .Output_mult(mult_chiffre_23_output_mult), .Output_reel(mult_chiffre_23_output_reel),
    .Input_mult(incrementeur_horloge_heure2_1_p2), .Reset(d_ff_2_q), .Clock_mult(Clk_horloge),
    .Clock_set(Set_heure), .Set_value(set_horloge_1_heures[6]), .Set_enable(and_50_out));
  mult_chiffre mult_chiffre_24 (
    .Output_mult(mult_chiffre_24_output_mult), .Output_reel(mult_chiffre_24_output_reel),
    .Input_mult(incrementeur_horloge_heure2_1_p3), .Reset(d_ff_2_q), .Clock_mult(Clk_horloge),
    .Clock_set(Set_heure), .Set_value(set_horloge_1_heures[7]), .Set_enable(and_50_out));
  mult_chiffre mult_chiffre_1 (
    .Output_mult(mult_chiffre_1_output_mult), .Output_reel(mult_chiffre_1_output_reel),
    .Input_mult(incrementeur_1_1_output_1), .Reset(d_ff_2_q), .Clock_mult(Clk_horloge),
    .Clock_set(Set_heure), .Set_value(set_horloge_1_secondes[0]), .Set_enable(and_50_out));
  mult_chiffre mult_chiffre_2 (
    .Output_mult(mult_chiffre_2_output_mult), .Output_reel(mult_chiffre_2_output_reel),
    .Input_mult(incrementeur_1_1_output_2), .Reset(d_ff_2_q), .Clock_mult(Clk_horloge),
    .Clock_set(Set_heure), .Set_value(set_horloge_1_secondes[1]), .Set_enable(and_50_out));
  mult_chiffre mult_chiffre_3 (
    .Output_mult(mult_chiffre_3_output_mult), .Output_reel(mult_chiffre_3_output_reel),
    .Input_mult(incrementeur_1_1_output_3), .Reset(d_ff_2_q), .Clock_mult(Clk_horloge),
    .Clock_set(Set_heure), .Set_value(set_horloge_1_secondes[2]), .Set_enable(and_50_out));
  mult_chiffre mult_chiffre_4 (
    .Output_mult(mult_chiffre_4_output_mult), .Output_reel(mult_chiffre_4_output_reel),
    .Input_mult(incrementeur_1_1_output_4), .Reset(d_ff_2_q), .Clock_mult(Clk_horloge),
    .Clock_set(Set_heure), .Set_value(set_horloge_1_secondes[3]), .Set_enable(and_50_out));
  and and_2 (and_2_out, mult_chiffre_5_output_mult, ~Mode_set);  // AND_Gate
  and and_3 (and_3_out, set_horloge_1_secondes[4], Mode_set);
  and and_4 (and_4_out, mult_chiffre_6_output_mult, ~Mode_set);  // AND_Gate
  and and_5 (and_5_out, set_horloge_1_secondes[5], Mode_set);
  and and_6 (and_6_out, mult_chiffre_7_output_mult, ~Mode_set);  // AND_Gate
  and and_7 (and_7_out, set_horloge_1_secondes[6], Mode_set);
  and and_8 (and_8_out, mult_chiffre_8_output_mult, ~Mode_set);  // AND_Gate
  and and_9 (and_9_out, set_horloge_1_secondes[7], Mode_set);
  and and_10 (and_10_out, mult_chiffre_1_output_mult, ~Mode_set);  // AND_Gate
  and and_11 (and_11_out, set_horloge_1_secondes[0], Mode_set);
  and and_12 (and_12_out, mult_chiffre_2_output_mult, ~Mode_set);  // AND_Gate
  and and_13 (and_13_out, set_horloge_1_secondes[1], Mode_set);
  and and_14 (and_14_out, mult_chiffre_3_output_mult, ~Mode_set);  // AND_Gate
  and and_15 (and_15_out, set_horloge_1_secondes[2], Mode_set);
  and and_16 (and_16_out, mult_chiffre_4_output_mult, ~Mode_set);  // AND_Gate
  and and_17 (and_17_out, set_horloge_1_secondes[3], Mode_set);
  and and_18 (and_18_out, mult_chiffre_13_output_mult, ~Mode_set);  // AND_Gate
  and and_19 (and_19_out, set_horloge_1_minutes[4], Mode_set);
  and and_20 (and_20_out, mult_chiffre_14_output_mult, ~Mode_set);  // AND_Gate
  and and_21 (and_21_out, set_horloge_1_minutes[5], Mode_set);
  and and_22 (and_22_out, mult_chiffre_15_output_mult, ~Mode_set);  // AND_Gate
  and and_23 (and_23_out, set_horloge_1_minutes[6], Mode_set);
  and and_24 (and_24_out, mult_chiffre_16_output_mult, ~Mode_set);  // AND_Gate
  and and_25 (and_25_out, set_horloge_1_minutes[7], Mode_set);
  or or_1 (Secondes[0], and_10_out, and_11_out);
  or or_2 (Secondes[1], and_12_out, and_13_out);
  or or_3 (Secondes[2], and_14_out, and_15_out);
  or or_4 (Secondes[3], and_16_out, and_17_out);
  or or_5 (Secondes[4], and_2_out, and_3_out);
  or or_6 (Secondes[5], and_4_out, and_5_out);
  or or_7 (Secondes[6], and_6_out, and_7_out);
  or or_8 (Secondes[7], and_8_out, and_9_out);
  and and_26 (and_26_out, mult_chiffre_9_output_mult, ~Mode_set);  // AND_Gate
  and and_27 (and_27_out, set_horloge_1_minutes[0], Mode_set);
  and and_28 (and_28_out, mult_chiffre_10_output_mult, ~Mode_set);  // AND_Gate
  and and_29 (and_29_out, set_horloge_1_minutes[1], Mode_set);
  and and_30 (and_30_out, mult_chiffre_11_output_mult, ~Mode_set);  // AND_Gate
  and and_31 (and_31_out, set_horloge_1_minutes[2], Mode_set);
  and and_32 (and_32_out, mult_chiffre_12_output_mult, ~Mode_set);  // AND_Gate
  and and_33 (and_33_out, set_horloge_1_minutes[3], Mode_set);
  and and_34 (and_34_out, mult_chiffre_17_output_mult, ~Mode_set);  // AND_Gate
  and and_35 (and_35_out, set_horloge_1_heures[0], Mode_set);
  and and_36 (and_36_out, mult_chiffre_18_output_mult, ~Mode_set);  // AND_Gate
  and and_37 (and_37_out, set_horloge_1_heures[1], Mode_set);
  and and_38 (and_38_out, mult_chiffre_19_output_mult, ~Mode_set);  // AND_Gate
  and and_39 (and_39_out, set_horloge_1_heures[2], Mode_set);
  and and_40 (and_40_out, mult_chiffre_20_output_mult, ~Mode_set);  // AND_Gate
  and and_41 (and_41_out, set_horloge_1_heures[3], Mode_set);
  and and_42 (and_42_out, mult_chiffre_21_output_mult, ~Mode_set);  // AND_Gate
  and and_43 (and_43_out, set_horloge_1_heures[4], Mode_set);
  and and_44 (and_44_out, mult_chiffre_22_output_mult, ~Mode_set);  // AND_Gate
  and and_45 (and_45_out, set_horloge_1_heures[5], Mode_set);
  and and_46 (and_46_out, mult_chiffre_23_output_mult, ~Mode_set);  // AND_Gate
  and and_47 (and_47_out, set_horloge_1_heures[6], Mode_set);
  and and_48 (and_48_out, mult_chiffre_24_output_mult, ~Mode_set);  // AND_Gate
  and and_49 (and_49_out, set_horloge_1_heures[7], Mode_set);
  or or_9 (Minutes[0], and_26_out, and_27_out);
  or or_10 (Minutes[1], and_28_out, and_29_out);
  or or_11 (Minutes[2], and_30_out, and_31_out);
  or or_12 (Minutes[3], and_32_out, and_33_out);
  or or_13 (Minutes[4], and_18_out, and_19_out);
  or or_14 (Minutes[5], and_20_out, and_21_out);
  or or_15 (Minutes[6], and_22_out, and_23_out);
  or or_16 (Minutes[7], and_24_out, and_25_out);
  or or_17 (Heures[4], and_42_out, and_43_out);
  or or_18 (Heures[5], and_44_out, and_45_out);
  or or_19 (Heures[6], and_46_out, and_47_out);
  or or_20 (Heures[7], and_48_out, and_49_out);
  or or_21 (Heures[0], and_34_out, and_35_out);
  or or_22 (Heures[1], and_36_out, and_37_out);
  or or_23 (Heures[2], and_38_out, and_39_out);
  or or_24 (Heures[3], and_40_out, and_41_out);
  set_horloge set_horloge_1 (
    .Mode_set(Mode_set), .CH_C(CH_C), .Decodeur(Encodeur), .Clock(Clk_bouton), .Reset(Reset),
    .Clk_encodeur(Clk_encodeur), .Secondes(set_horloge_1_secondes), .Minutes(set_horloge_1_minutes),
    .Heures(set_horloge_1_heures), .Retour_horloge(retour_horloge), .Mode_sec(Mode_sec), .Mode_min(Mode_min),
    .Mode_heure(Mode_heure));
  and and_50 (and_50_out, Mode_set, retour_horloge);

  // Other names for the same wires on the sheet: chanel_c = CH_C

  // Notes on the sheet:
  //   secondes_1
  //   secondes_2
  //   minutes_1
  //   minutes_2
  //   heures
  //   heures
endmodule

module set_menu (
  input  Clock,
  input  Clock_bouton,
  input  CH_C,
  input  [1:0] Encodeur,
  input  Start_chrono,
  input  Alarme_on,
  input  Reset,
  input  [7:0] Secondes_reel,
  input  [7:0] Minutes_reel,
  input  [7:0] Heures_reel,
  input  Reset_chrono,
  input  Input_1,
  input  Input_2,
  input  Input_3,
  input  Input_4,
  input  Input_5,
  input  Input_6,
  input  Input_7,
  input  Start_fonction_complexe,
  input  Re,
  input  Mi,
  input  Fa_diese,
  input  Sol,
  input  La,
  input  Si,
  input  Do,
  input  Re_haut,
  input  Do_bas,
  input  Fa,
  input  Clock_message,
  input  Clock_musique,
  input  Clock_jeu,
  input  Clk_encodeur,
  input  [1:0] Enable_message,
  input  [1:0] Enable_musique,
  output [7:0] Secondes,
  output [7:0] Minutes,
  output [7:0] Heures,
  output Buzzer,
  output Mode_abc,
  output [2:0] Fonctions_on,
  output Fonction_complexe,
  output [6:0] LED,
  output [6:0] Letter_1,
  output [6:0] Letter_2,
  output [6:0] Letter_3,
  output [6:0] Letter_4,
  output [6:0] Letter_5,
  output [6:0] Letter_6,
  output Set_song,
  output Mode_sec,
  output Mode_min,
  output Mode_heure,
  output Fonction_enable
);

  wire affichage_alarme_1_buzzer, affichage_decompteur_1_buzzer, and_1_out, and_2_out, and_3_out, and_4_out,
       and_5_out, and_6_out, and_7_out, and_8_out, and_9_out, fonction_enable_t, jeu_1_buzzer,
       message_musique_1_buzzer, mode_heure_t, mode_min_t, mode_sec_t, or_1_out, or_3_out, set_jeu;
  wire [3:0] affichage;
  wire [6:0] jeu_1_c, jeu_1_e, jeu_1_led_1, jeu_1_s, jeu_1_u, message_musique_1_leds,
       message_musique_1_letter_1, message_musique_1_letter_2, message_musique_1_letter_3,
       message_musique_1_letter_4, message_musique_1_letter_5, message_musique_1_letter_6;
  wire [7:0] affichage_alarme_1_heures, affichage_alarme_1_minutes, affichage_alarme_1_secondes,
       affichage_decompteur_1_heures, affichage_decompteur_1_minutes, affichage_decompteur_1_secondes,
       chrono_compteur_1_heures, chrono_compteur_1_minutes, chrono_compteur_1_secondes, multiplexer_7_out,
       multiplexer_9_out, multiplexer_10_out;

  compteur_complet compteur_complet_1 (
    .CH_C(CH_C), .Encodeur(Encodeur), .Clock_bouton(Clock_bouton), .Reset(Reset),
    .Clk_encodeur(Clk_encodeur), .Set_alarme(Fonctions_on[0]), .Set_chrono(Fonctions_on[1]),
    .Set_decompteur(Fonctions_on[2]), .Set_song(Set_song), .Set_jeu(set_jeu), .Affichage_menu(affichage),
    .Mode_sec(mode_sec_t), .Mode_min(mode_min_t), .Mode_heure(mode_heure_t), .Fct_enable(fonction_enable_t),
    .Mode_menu(Mode_abc));
  affichage_alarme affichage_alarme_1 (
    .Set_alarme(Fonctions_on[0]), .Encodeur(Encodeur), .Clock_encodeur(Clk_encodeur),
    .Mode_secondes(mode_sec_t), .Mode_minutes(mode_min_t), .Mode_heures(mode_heure_t), .Alarme_on(Alarme_on),
    .Reset(Reset), .Secondes_reel(Secondes_reel), .Minutes_reel(Minutes_reel), .Heures_reel(Heures_reel),
    .Secondes(affichage_alarme_1_secondes), .Minutes(affichage_alarme_1_minutes),
    .Heures(affichage_alarme_1_heures), .Buzzer(affichage_alarme_1_buzzer));
  chrono_compteur chrono_compteur_1 (
    .Chrono_on(Fonctions_on[1]), .Start_stop(Start_chrono), .Reset_asynchrone(Reset_chrono), .Clock(Clock),
    .Reset_general(Reset), .Secondes(chrono_compteur_1_secondes), .Minutes(chrono_compteur_1_minutes),
    .Heures(chrono_compteur_1_heures));
  affichage_decompteur affichage_decompteur_1 (
    .Set_decompteur(Fonctions_on[2]), .Encodeur(Encodeur), .Clk_encodeur(Clock_bouton),
    .Mode_secondes(mode_sec_t), .Mode_minutes(mode_min_t), .Mode_heures(mode_heure_t),
    .Function_initiate(fonction_enable_t), .Clock(Clock), .Reset(Reset), .Start_stop(Start_chrono),
    .Stop_alarme(Reset_chrono), .Secondes(affichage_decompteur_1_secondes),
    .Minutes(affichage_decompteur_1_minutes), .Heures(affichage_decompteur_1_heures),
    .Buzzer(affichage_decompteur_1_buzzer));
  message_musique message_musique_1 (
    .Enable(Set_song), .Enable_message(Enable_message), .Enable_musique(Enable_musique), .Reset(Reset),
    .Clock_message(Clock_message), .Clock_bouton(Clock_bouton), .Clock_musique(Clock_musique), .Re(Re),
    .Mi(Mi), .Fa_diese(Fa_diese), .Sol(Sol), .La(La), .Si(Si), .Do(Do), .Re_haut(Re_haut), .Do_bas(Do_bas),
    .Fa(Fa), .Letter_1(message_musique_1_letter_1), .Letter_2(message_musique_1_letter_2),
    .Letter_3(message_musique_1_letter_3), .Letter_4(message_musique_1_letter_4),
    .Letter_5(message_musique_1_letter_5), .Letter_6(message_musique_1_letter_6),
    .Buzzer(message_musique_1_buzzer), .LEDS(message_musique_1_leds));
  jeu jeu_1 (
    .Enable(set_jeu), .Start(Start_fonction_complexe), .Input_1(Input_1), .Input_2(Input_2),
    .Input_3(Input_3), .Input_4(Input_4), .Input_5(Input_5), .Input_6(Input_6), .Input_7(Input_7), .Do(Do),
    .Sol(Sol), .La(La), .Si(Si), .Reset(Reset), .Clock_musique_jeu(Clock_musique), .Clock_jeu(Clock_jeu),
    .LED_1(jeu_1_led_1[0]), .LED_2(jeu_1_led_1[1]), .LED_3(jeu_1_led_1[2]), .LED_4(jeu_1_led_1[3]),
    .LED_5(jeu_1_led_1[4]), .LED_6(jeu_1_led_1[5]), .LED_7(jeu_1_led_1[6]), .s(jeu_1_s), .u(jeu_1_u),
    .c(jeu_1_c), .e(jeu_1_e), .Buzzer(jeu_1_buzzer));
  or or_1 (or_1_out, affichage_alarme_1_buzzer, affichage_decompteur_1_buzzer);
  assign LED = message_musique_1_leds | jeu_1_led_1;  // OR_Gate or_2, 7 bits wide
  or or_3 (or_3_out, message_musique_1_buzzer, jeu_1_buzzer);
  Multiplexer #(.width(7)) multiplexer_1 (
    .in0(message_musique_1_letter_1), .in1(jeu_1_s), .out(Letter_1), .sel(set_jeu));
  Multiplexer #(.width(7)) multiplexer_2 (
    .in0(message_musique_1_letter_2), .in1(jeu_1_e), .out(Letter_2), .sel(set_jeu));
  Multiplexer #(.width(7)) multiplexer_3 (
    .in0(message_musique_1_letter_3), .in1(jeu_1_c), .out(Letter_3), .sel(set_jeu));
  Multiplexer #(.width(7)) multiplexer_4 (
    .in0(message_musique_1_letter_4), .in1(jeu_1_c), .out(Letter_4), .sel(set_jeu));
  Multiplexer #(.width(7)) multiplexer_5 (
    .in0(message_musique_1_letter_5), .in1(jeu_1_u), .out(Letter_5), .sel(set_jeu));
  Multiplexer #(.width(7)) multiplexer_6 (
    .in0(message_musique_1_letter_6), .in1(jeu_1_s), .out(Letter_6), .sel(set_jeu));
  Multiplexer #(.select(3), .width(8)) multiplexer_7 (
    .in0({8{1'b0}}), .in1(affichage_alarme_1_secondes), .in2(chrono_compteur_1_secondes), .in3({8{1'b0}}),
    .in4(affichage_decompteur_1_secondes), .in5({8{1'b0}}), .in6({8{1'b0}}), .in7({8{1'b0}}),
    .out(multiplexer_7_out), .sel(Fonctions_on));
  and and_1 (and_1_out, Fonctions_on[2], mode_sec_t);
  and and_2 (and_2_out, mode_sec_t, Fonctions_on[0]);
  and and_3 (and_3_out, Fonctions_on[2], mode_min_t);
  and and_4 (and_4_out, mode_min_t, Fonctions_on[0]);
  and and_5 (and_5_out, Fonctions_on[2], mode_heure_t);
  and and_6 (and_6_out, mode_heure_t, Fonctions_on[0]);
  and and_7 (and_7_out, Fonctions_on[2], fonction_enable_t);
  and and_8 (and_8_out, fonction_enable_t, Fonctions_on[0]);
  Multiplexer #(.width(8)) multiplexer_8 (
    .in0(multiplexer_7_out), .in1({4'b0000, affichage}), .out(Secondes), .sel(Mode_abc));
  Multiplexer #(.select(3), .width(8)) multiplexer_9 (
    .in0({8{1'b0}}), .in1(affichage_alarme_1_heures), .in2(chrono_compteur_1_heures), .in3({8{1'b0}}),
    .in4(affichage_decompteur_1_heures), .in5({8{1'b0}}), .in6({8{1'b0}}), .in7({8{1'b0}}),
    .out(multiplexer_9_out), .sel(Fonctions_on));
  and and_9 (and_9_out, or_1_out, Clock, La);
  or or_4 (Mode_sec, and_1_out, and_2_out);
  or or_5 (Mode_min, and_3_out, and_4_out);
  or or_6 (Mode_heure, and_5_out, and_6_out);
  or or_7 (Fonction_enable, and_7_out, and_8_out);
  Multiplexer #(.select(3), .width(8)) multiplexer_10 (
    .in0({8{1'b0}}), .in1(affichage_alarme_1_minutes), .in2(chrono_compteur_1_minutes), .in3({8{1'b0}}),
    .in4(affichage_decompteur_1_minutes), .in5({8{1'b0}}), .in6({8{1'b0}}), .in7({8{1'b0}}),
    .out(multiplexer_10_out), .sel(Fonctions_on));
  Multiplexer #(.width(8)) multiplexer_11 (.in0(multiplexer_9_out), .in1({8{1'b0}}), .out(Heures), .sel(Mode_abc));
  or or_8 (Fonction_complexe, set_jeu, Set_song);
  Multiplexer #(.width(8)) multiplexer_12 (.in0(multiplexer_10_out), .in1({8{1'b0}}), .out(Minutes), .sel(Mode_abc));
  Multiplexer multiplexer_13 (.in0(and_9_out), .in1(or_3_out), .out(Buzzer), .sel(Fonction_complexe));

  // Other names for the same wires on the sheet: clk_bouton = Clock_bouton; dip_switch_4 = Input_1;
  //   dip_switch_5 = Input_2; dip_switch_6 = Input_3; dip_switch_7 = Input_4; dip_switch_8 = Input_5;
  //   dip_switch_9 = Input_6; dip_switch_10 = Input_7; fonction_on[2:0] = Fonctions_on; mode_menu = Mode_abc;
  //   start_stop = Start_chrono
endmodule

module set_horloge (
  input  Mode_set,
  input  CH_C,
  input  [1:0] Decodeur,
  input  Clock,
  input  Reset,
  input  Clk_encodeur,
  output [7:0] Secondes,
  output [7:0] Minutes,
  output [7:0] Heures,
  output Retour_horloge,
  output Mode_sec,
  output Mode_min,
  output Mode_heure
);

  wire and_2_out, and_3_out, compteur_chanel_c_1_mode_menu;
  wire [7:0] set_valeur_1_nbr, set_valeur_2_nbr, set_valeur_heures_1_nbr;

  and and_1 (Mode_sec, compteur_chanel_c_1_mode_menu, Mode_set);
  and and_2 (and_2_out, Mode_min, Mode_set);
  and and_3 (and_3_out, Mode_heure, Mode_set);
  compteur_chanel_c compteur_chanel_c_1 (
    .CH_C(CH_C), .Clock(Clock), .Chrono_selected(1'b0), .Reset_input(Reset),
    .Mode_menu(compteur_chanel_c_1_mode_menu), .Ajuster_sec(Mode_min), .Ajuster_min(Mode_heure),
    .Ajuster_heures(Retour_horloge));  // open: Fonction_enable, Reset
  set_valeur set_valeur_1 (
    .Enable(Mode_sec), .Encodeur(Decodeur), .Reset(Reset), .Clock(Clk_encodeur), .Nbr(set_valeur_1_nbr));
  set_valeur set_valeur_2 (
    .Enable(and_2_out), .Encodeur(Decodeur), .Reset(Reset), .Clock(Clk_encodeur), .Nbr(set_valeur_2_nbr));
  set_valeur_heures set_valeur_heures_1 (
    .Enable(and_3_out), .Decodeur(Decodeur), .Reset(Reset), .Clock(Clk_encodeur),
    .Nbr(set_valeur_heures_1_nbr));
  valeur_memory valeur_memory_1 (
    .Valeur(set_valeur_1_nbr), .Garde_memoire(Mode_sec), .Clock(Clock), .Reset(Reset), .Output_bus_1(Secondes));
  valeur_memory valeur_memory_2 (
    .Valeur(set_valeur_2_nbr), .Garde_memoire(and_2_out), .Clock(Clock), .Reset(Reset), .Output_bus_1(Minutes));
  valeur_memory valeur_memory_3 (
    .Valeur(set_valeur_heures_1_nbr), .Garde_memoire(and_3_out), .Clock(Clock), .Reset(Reset),
    .Output_bus_1(Heures));
endmodule

module number_clock (
  input  [3:0] nbr,
  input  function_complexe,
  input  [6:0] letter
);

  wire multiplexer_1_out, multiplexer_2_out, multiplexer_3_out, multiplexer_4_out, multiplexer_5_out,
       multiplexer_6_out, multiplexer_7_out, number_1_a_out, number_1_b_out, number_1_c_out, number_1_d_out,
       number_1_e_out, number_1_f_out, number_1_g_out;

  number number_1 (
    .nbr(nbr), .a_out(number_1_a_out), .b_out(number_1_b_out), .c_out(number_1_c_out),
    .d_out(number_1_d_out), .e_out(number_1_e_out), .f_out(number_1_f_out), .g_out(number_1_g_out));
  Multiplexer multiplexer_1 (.in0(number_1_a_out), .in1(letter[0]), .out(multiplexer_1_out), .sel(function_complexe));
  Multiplexer multiplexer_2 (.in0(number_1_b_out), .in1(letter[1]), .out(multiplexer_2_out), .sel(function_complexe));
  Multiplexer multiplexer_3 (.in0(number_1_c_out), .in1(letter[2]), .out(multiplexer_3_out), .sel(function_complexe));
  Multiplexer multiplexer_4 (.in0(number_1_d_out), .in1(letter[3]), .out(multiplexer_4_out), .sel(function_complexe));
  Multiplexer multiplexer_5 (.in0(number_1_e_out), .in1(letter[4]), .out(multiplexer_5_out), .sel(function_complexe));
  Multiplexer multiplexer_6 (.in0(number_1_f_out), .in1(letter[5]), .out(multiplexer_6_out), .sel(function_complexe));
  Multiplexer multiplexer_7 (.in0(number_1_g_out), .in1(letter[6]), .out(multiplexer_7_out), .sel(function_complexe));
  _7_Segment_Display L_7_Segment_Display_6 (
    .g(multiplexer_7_out), .f(multiplexer_6_out), .a(multiplexer_1_out), .b(multiplexer_2_out),
    .e(multiplexer_5_out), .d(multiplexer_4_out), .c(multiplexer_3_out), .dp(1'b0));
endmodule

module incrementeur_1 (
  input  Input_1,
  input  Input_2,
  input  Input_3,
  input  Input_4,
  output Output_1,
  output Output_2,
  output Output_3,
  output Output_4,
  output Carry_out
);

  wire additioneur_1_y0, additioneur_1_y1, additioneur_1_y2, additioneur_1_y3;

  additioneur additioneur_1 (
    .A0(Input_1), .B0(1'b1), .A1(Input_2), .B1(1'b0), .A2(Input_3), .B2(1'b0), .A3(Input_4), .B3(1'b0),
    .carry_in(1'b0), .Y0(additioneur_1_y0), .Y1(additioneur_1_y1), .Y2(additioneur_1_y2),
    .Y3(additioneur_1_y3), .Carry_out(Carry_out));
  and and_1 (Output_1, additioneur_1_y0, ~Carry_out);  // AND_Gate
  and and_2 (Output_2, additioneur_1_y1, ~Carry_out);  // AND_Gate
  and and_3 (Output_3, additioneur_1_y2, ~Carry_out);  // AND_Gate
  and and_4 (Output_4, additioneur_1_y3, ~Carry_out);  // AND_Gate
endmodule

module incrementeur_horloge (
  input  Y0,
  input  Y1,
  input  Y2,
  input  Y3,
  input  Carry_in,
  output P0,
  output P1,
  output P2,
  output P3,
  output Carry_out
);

  wire additioneur_1_y0, additioneur_1_y1, additioneur_1_y2, additioneur_1_y3, and_1_out, and_2_out,
       and_3_out, and_4_out, and_5_out, and_6_out, and_7_out, and_8_out, and_9_out, and_10_out, and_11_out,
       and_12_out;

  additioneur additioneur_1 (
    .A0(Y0), .B0(1'b0), .A1(Y1), .B1(1'b0), .A2(Y2), .B2(1'b0), .A3(Y3), .B3(1'b0), .carry_in(Carry_in),
    .Y0(additioneur_1_y0), .Y1(additioneur_1_y1), .Y2(additioneur_1_y2), .Y3(additioneur_1_y3),
    .Carry_out(Carry_out));
  and and_1 (and_1_out, additioneur_1_y0, ~Carry_out);  // AND_Gate
  and and_2 (and_2_out, additioneur_1_y1, ~Carry_out);  // AND_Gate
  and and_3 (and_3_out, additioneur_1_y2, ~Carry_out);  // AND_Gate
  and and_4 (and_4_out, additioneur_1_y3, ~Carry_out);  // AND_Gate
  and and_5 (and_5_out, Y0, ~Carry_in);  // AND_Gate
  and and_6 (and_6_out, and_1_out, Carry_in);
  and and_7 (and_7_out, Y1, ~Carry_in);  // AND_Gate
  and and_8 (and_8_out, and_2_out, Carry_in);
  and and_9 (and_9_out, Y2, ~Carry_in);  // AND_Gate
  and and_10 (and_10_out, and_3_out, Carry_in);
  and and_11 (and_11_out, Y3, ~Carry_in);  // AND_Gate
  and and_12 (and_12_out, and_4_out, Carry_in);
  or or_1 (P0, and_5_out, and_6_out);
  or or_2 (P1, and_7_out, and_8_out);
  or or_3 (P2, and_9_out, and_10_out);
  or or_4 (P3, and_11_out, and_12_out);

  // Notes on the sheet:
  //   si pas de carry in on incremente pas, si un carry out la sortie est à 0
endmodule

module incrementeur_horloge_min1 (
  input  Y0,
  input  Y1,
  input  Y2,
  input  Y3,
  input  Carry_in,
  output P0,
  output P1,
  output P2,
  output P3,
  output Carry_out
);

  wire additioneur_1_carry_out, additioneur_1_y0, additioneur_1_y1, additioneur_1_y2, additioneur_1_y3,
       and_1_out, and_2_out, and_3_out, and_4_out, and_5_out, and_6_out, and_7_out, and_8_out, and_9_out,
       and_10_out, and_11_out, and_12_out, and_13_out, not_1_out, not_2_out, or_2_out, or_3_out, or_4_out,
       or_5_out;

  additioneur additioneur_1 (
    .A0(Y0), .B0(1'b0), .A1(Y1), .B1(1'b0), .A2(Y2), .B2(1'b0), .A3(Y3), .B3(1'b0), .carry_in(Carry_in),
    .Y0(additioneur_1_y0), .Y1(additioneur_1_y1), .Y2(additioneur_1_y2), .Y3(additioneur_1_y3),
    .Carry_out(additioneur_1_carry_out));
  not not_1 (not_1_out, or_2_out);
  not not_2 (not_2_out, or_5_out);
  or or_1 (Carry_out, additioneur_1_carry_out, and_1_out);
  and and_1 (and_1_out, not_1_out, or_3_out, or_4_out, not_2_out);
  and and_2 (and_2_out, additioneur_1_y0, ~additioneur_1_carry_out);  // AND_Gate
  and and_3 (and_3_out, additioneur_1_y1, ~additioneur_1_carry_out);  // AND_Gate
  and and_4 (and_4_out, additioneur_1_y2, ~additioneur_1_carry_out);  // AND_Gate
  and and_5 (and_5_out, additioneur_1_y3, ~additioneur_1_carry_out);  // AND_Gate
  and and_6 (and_6_out, Y0, ~Carry_in);  // AND_Gate
  and and_7 (and_7_out, and_2_out, Carry_in);
  and and_8 (and_8_out, Y1, ~Carry_in);  // AND_Gate
  and and_9 (and_9_out, and_3_out, Carry_in);
  and and_10 (and_10_out, Y2, ~Carry_in);  // AND_Gate
  and and_11 (and_11_out, and_4_out, Carry_in);
  and and_12 (and_12_out, Y3, ~Carry_in);  // AND_Gate
  and and_13 (and_13_out, and_5_out, Carry_in);
  or or_2 (or_2_out, and_6_out, and_7_out);
  or or_3 (or_3_out, and_8_out, and_9_out);
  or or_4 (or_4_out, and_10_out, and_11_out);
  or or_5 (or_5_out, and_12_out, and_13_out);
  and and_14 (P0, or_2_out, ~and_1_out);  // AND_Gate
  and and_15 (P1, or_3_out, ~and_1_out);  // AND_Gate
  and and_16 (P2, or_4_out, ~and_1_out);  // AND_Gate
  and and_17 (P3, or_5_out, ~and_1_out);  // AND_Gate

  // Notes on the sheet:
  //   si pas de carry in on incremente pas, si un carry out la sortie est à 0
endmodule

module incrementeur_horloge_heure1 (
  input  Y0,
  input  Y1,
  input  Y2,
  input  Y3,
  input  Carry_in,
  input  If_2,
  output P0,
  output P1,
  output P2,
  output P3,
  output Carry_out,
  output Reset
);

  wire additioneur_1_carry_out, additioneur_1_y0, additioneur_1_y1, additioneur_1_y2, additioneur_1_y3,
       and_2_out, and_3_out, and_4_out, and_5_out, and_6_out, and_7_out, and_8_out, and_9_out, and_10_out,
       and_11_out, and_12_out, and_13_out, not_1_out, not_2_out, not_3_out, or_2_out, or_3_out, or_4_out,
       or_5_out;

  additioneur additioneur_1 (
    .A0(Y0), .B0(1'b0), .A1(Y1), .B1(1'b0), .A2(Y2), .B2(1'b0), .A3(Y3), .B3(1'b0), .carry_in(Carry_in),
    .Y0(additioneur_1_y0), .Y1(additioneur_1_y1), .Y2(additioneur_1_y2), .Y3(additioneur_1_y3),
    .Carry_out(additioneur_1_carry_out));
  not not_1 (not_1_out, or_2_out);
  not not_2 (not_2_out, or_3_out);
  not not_3 (not_3_out, or_5_out);
  or or_1 (Carry_out, additioneur_1_carry_out, Reset);
  and and_1 (Reset, not_1_out, not_2_out, If_2, or_4_out, not_3_out);
  and and_2 (and_2_out, additioneur_1_y0, ~additioneur_1_carry_out);  // AND_Gate
  and and_3 (and_3_out, additioneur_1_y1, ~additioneur_1_carry_out);  // AND_Gate
  and and_4 (and_4_out, additioneur_1_y2, ~additioneur_1_carry_out);  // AND_Gate
  and and_5 (and_5_out, additioneur_1_y3, ~additioneur_1_carry_out);  // AND_Gate
  and and_6 (and_6_out, Y0, ~Carry_in);  // AND_Gate
  and and_7 (and_7_out, and_2_out, Carry_in);
  and and_8 (and_8_out, Y1, ~Carry_in);  // AND_Gate
  and and_9 (and_9_out, and_3_out, Carry_in);
  and and_10 (and_10_out, Y2, ~Carry_in);  // AND_Gate
  and and_11 (and_11_out, and_4_out, Carry_in);
  and and_12 (and_12_out, Y3, ~Carry_in);  // AND_Gate
  and and_13 (and_13_out, and_5_out, Carry_in);
  or or_2 (or_2_out, and_6_out, and_7_out);
  or or_3 (or_3_out, and_8_out, and_9_out);
  or or_4 (or_4_out, and_10_out, and_11_out);
  or or_5 (or_5_out, and_12_out, and_13_out);
  and and_14 (P0, or_2_out, ~Reset);  // AND_Gate
  and and_15 (P1, or_3_out, ~Reset);  // AND_Gate
  and and_16 (P2, or_4_out, ~Reset);  // AND_Gate
  and and_17 (P3, or_5_out, ~Reset);  // AND_Gate

  // Notes on the sheet:
  //   si pas de carry in on incremente pas, si un carry out la sortie est à 0
endmodule

module incrementeur_horloge_heure2 (
  input  Y0,
  input  Y1,
  input  Y2,
  input  Y3,
  input  Carry_in,
  output P0,
  output P1,
  output P2,
  output P3,
  output Carry_out,
  output if_2
);

  wire additioneur_1_y0, additioneur_1_y1, additioneur_1_y2, additioneur_1_y3, and_1_out, and_2_out,
       and_3_out, and_4_out, and_5_out, and_6_out, and_7_out, and_8_out, and_9_out, and_10_out, and_11_out,
       and_12_out, not_1_out, not_2_out, not_3_out;

  additioneur additioneur_1 (
    .A0(Y0), .B0(1'b0), .A1(Y1), .B1(1'b0), .A2(Y2), .B2(1'b0), .A3(Y3), .B3(1'b0), .carry_in(Carry_in),
    .Y0(additioneur_1_y0), .Y1(additioneur_1_y1), .Y2(additioneur_1_y2), .Y3(additioneur_1_y3),
    .Carry_out(Carry_out));
  and and_1 (and_1_out, additioneur_1_y0, ~Carry_out);  // AND_Gate
  and and_2 (and_2_out, additioneur_1_y1, ~Carry_out);  // AND_Gate
  and and_3 (and_3_out, additioneur_1_y2, ~Carry_out);  // AND_Gate
  and and_4 (and_4_out, additioneur_1_y3, ~Carry_out);  // AND_Gate
  and and_5 (and_5_out, Y0, ~Carry_in);  // AND_Gate
  and and_6 (and_6_out, and_1_out, Carry_in);
  and and_7 (and_7_out, Y1, ~Carry_in);  // AND_Gate
  and and_8 (and_8_out, and_2_out, Carry_in);
  and and_9 (and_9_out, Y2, ~Carry_in);  // AND_Gate
  and and_10 (and_10_out, and_3_out, Carry_in);
  and and_11 (and_11_out, Y3, ~Carry_in);  // AND_Gate
  and and_12 (and_12_out, and_4_out, Carry_in);
  or or_1 (P0, and_5_out, and_6_out);
  or or_2 (P1, and_7_out, and_8_out);
  or or_3 (P2, and_9_out, and_10_out);
  or or_4 (P3, and_11_out, and_12_out);
  not not_1 (not_1_out, P0);
  and and_13 (if_2, not_1_out, P1, not_2_out, not_3_out);
  not not_2 (not_2_out, P2);
  not not_3 (not_3_out, P3);

  // Notes on the sheet:
  //   si pas de carry in on incremente pas, si un carry out la sortie est à 0
endmodule

module mult_chiffre (
  input  Input_mult,
  input  Reset,
  input  Clock_mult,
  input  Clock_set,
  input  Set_value,
  input  Set_enable,
  output Output_mult,
  output Output_reel
);

  wire and_1_out, and_2_out, and_3_out, d_ff_2_q, or_1_out, or_2_out;

  and and_1 (and_1_out, ~Set_value, Set_enable);  // AND_Gate
  or or_1 (or_1_out, Reset, and_1_out);
  D_Flip_Flop d_ff_1 (.D(Input_mult), .clk(Clock_mult), .Q(Output_mult), .preset(1'b0), .reset(or_1_out));  // open: Qn
  D_Flip_Flop d_ff_2 (.D(Input_mult), .clk(Clock_mult), .Q(d_ff_2_q), .preset(1'b0), .reset(or_1_out));  // open: Qn
  or or_2 (or_2_out, Clock_set, Set_enable);
  and and_2 (and_2_out, d_ff_2_q, ~or_2_out);  // AND_Gate
  and and_3 (and_3_out, Set_value, or_2_out);
  or or_3 (Output_reel, and_2_out, and_3_out);
endmodule

module affichage_alarme (
  input  Set_alarme,
  input  [1:0] Encodeur,
  input  Clock_encodeur,
  input  Mode_secondes,
  input  Mode_minutes,
  input  Mode_heures,
  input  Alarme_on,
  input  Reset,
  input  [7:0] Secondes_reel,
  input  [7:0] Minutes_reel,
  input  [7:0] Heures_reel,
  output [7:0] Secondes,
  output [7:0] Minutes,
  output [7:0] Heures,
  output Buzzer
);

  wire and_1_out, and_2_out, and_3_out;
  wire [7:0] set_valeur_1_nbr, set_valeur_2_nbr, set_valeur_heures_1_nbr;

  and and_1 (and_1_out, Mode_secondes, Set_alarme);
  and and_2 (and_2_out, Set_alarme, Mode_minutes);
  and and_3 (and_3_out, Set_alarme, Mode_heures);
  set_valeur set_valeur_1 (
    .Enable(and_1_out), .Encodeur(Encodeur), .Reset(Reset), .Clock(Clock_encodeur), .Nbr(set_valeur_1_nbr));
  set_valeur set_valeur_2 (
    .Enable(and_2_out), .Encodeur(Encodeur), .Reset(Reset), .Clock(Clock_encodeur), .Nbr(set_valeur_2_nbr));
  set_valeur_heures set_valeur_heures_1 (
    .Enable(and_3_out), .Decodeur(Encodeur), .Reset(Reset), .Clock(Clock_encodeur),
    .Nbr(set_valeur_heures_1_nbr));
  valeur_memory valeur_memory_1 (
    .Valeur(set_valeur_1_nbr), .Garde_memoire(Mode_secondes), .Clock(Clock_encodeur), .Reset(Reset),
    .Output_bus_1(Secondes));
  valeur_memory valeur_memory_2 (
    .Valeur(set_valeur_2_nbr), .Garde_memoire(Mode_minutes), .Clock(Clock_encodeur), .Reset(Reset),
    .Output_bus_1(Minutes));
  valeur_memory valeur_memory_3 (
    .Valeur(set_valeur_heures_1_nbr), .Garde_memoire(Mode_heures), .Clock(Clock_encodeur), .Reset(Reset),
    .Output_bus_1(Heures));
  alarme alarme_1 (
    .Alarme_on(Alarme_on), .secondes(Secondes), .secondes_reel(Secondes_reel), .minutes(Minutes),
    .minutes_reel(Minutes_reel), .heures(Heures), .heures_real(Heures_reel), .clock(Clock_encodeur),
    .Reset(Reset), .Buzzer(Buzzer));

  // Other names for the same wires on the sheet: clk_encodeur = Clock_encodeur
endmodule

module chrono_compteur (
  input  Chrono_on,
  input  Start_stop,
  input  Reset_asynchrone,
  input  Clock,
  input  Reset_general,
  output [7:0] Secondes,
  output [7:0] Minutes,
  output [7:0] Heures
);

  wire and_1_out, and_2_out, and_3_out, and_4_out, and_5_out, and_6_out, and_7_out, and_8_out, and_9_out,
       and_10_out, and_11_out, and_12_out, and_13_out, and_14_out, and_15_out, and_16_out, and_17_out,
       and_18_out, and_19_out, and_20_out, and_21_out, and_22_out, or_1_out;

  or or_1 (or_1_out, Reset_asynchrone, and_22_out);
  and and_1 (and_1_out, Start_stop, Chrono_on);
  and and_2 (and_2_out, and_13_out, and_12_out, Start_stop, Chrono_on);
  and and_3 (and_3_out, and_7_out, and_14_out, Start_stop, Chrono_on);
  and and_4 (and_4_out, and_8_out, and_15_out, Start_stop, Chrono_on);
  and and_5 (and_5_out, and_9_out, and_19_out, Start_stop, Chrono_on);
  and and_6 (and_6_out, and_10_out, and_20_out, Start_stop, Chrono_on);
  Counter #(.max('h9), .width(4)) counter_1 (
    .clr(Reset_general), .load(or_1_out), .up(1'b1), .count(and_1_out), .clk(Clock), .D(4'b0000),
    .Q(Secondes[3:0]));  // open: carry
  Counter #(.max('h5), .width(4)) counter_2 (
    .clr(Reset_general), .load(or_1_out), .up(1'b1), .count(and_2_out), .clk(Clock), .D(4'b0000),
    .Q(Secondes[7:4]));  // open: carry
  Counter #(.max('h9), .width(4)) counter_3 (
    .clr(Reset_general), .load(or_1_out), .up(1'b1), .count(and_3_out), .clk(Clock), .D(4'b0000),
    .Q(Minutes[3:0]));  // open: carry
  Counter #(.max('h5), .width(4)) counter_4 (
    .clr(Reset_general), .load(or_1_out), .up(1'b1), .count(and_4_out), .clk(Clock), .D(4'b0000),
    .Q(Minutes[7:4]));  // open: carry
  Counter #(.max('h9), .width(4)) counter_5 (
    .clr(Reset_general), .load(or_1_out), .up(1'b1), .count(and_5_out), .clk(Clock), .D(4'b0000),
    .Q(Heures[3:0]));  // open: carry
  Counter #(.max('h2), .width(4)) counter_6 (
    .clr(Reset_general), .load(or_1_out), .up(1'b1), .count(and_6_out), .clk(Clock), .D(4'b0000),
    .Q(Heures[7:4]));  // open: carry
  and and_7 (and_7_out, and_13_out, and_11_out);
  and and_8 (and_8_out, and_7_out, and_16_out);
  and and_9 (and_9_out, and_8_out, and_17_out);
  and and_10 (and_10_out, and_9_out, and_20_out);
  and and_11 (and_11_out, Secondes[4], ~Secondes[5], Secondes[6], ~Secondes[7]);  // AND_Gate
  and and_12 (and_12_out, Secondes[0], ~Secondes[1], ~Secondes[2], Secondes[3]);  // AND_Gate
  and and_13 (and_13_out, Secondes[0], ~Secondes[1], ~Secondes[2], Secondes[3]);  // AND_Gate
  and and_14 (and_14_out, Secondes[4], ~Secondes[5], Secondes[6], ~Secondes[7]);  // AND_Gate
  and and_15 (and_15_out, Minutes[0], ~Minutes[1], ~Minutes[2], Minutes[3]);  // AND_Gate
  and and_16 (and_16_out, Minutes[0], ~Minutes[1], ~Minutes[2], Minutes[3]);  // AND_Gate
  and and_17 (and_17_out, Minutes[4], ~Minutes[5], Minutes[6], ~Minutes[7]);  // AND_Gate
  and and_18 (and_18_out, ~Heures[4], Heures[5], ~Heures[6], ~Heures[7]);  // AND_Gate
  and and_19 (and_19_out, Minutes[4], ~Minutes[5], Minutes[6], ~Minutes[7]);  // AND_Gate
  and and_20 (and_20_out, Heures[0], ~Heures[1], ~Heures[2], Heures[3]);  // AND_Gate
  and and_21 (and_21_out, Heures[0], Heures[1], ~Heures[2], ~Heures[3], ~and_9_out);  // AND_Gate
  and and_22 (and_22_out, and_21_out, and_18_out);
endmodule

module affichage_decompteur (
  input  Set_decompteur,
  input  [1:0] Encodeur,
  input  Clk_encodeur,
  input  Mode_secondes,
  input  Mode_minutes,
  input  Mode_heures,
  input  Function_initiate,
  input  Clock,
  input  Reset,
  input  Start_stop,
  input  Stop_alarme,
  output [7:0] Secondes,
  output [7:0] Minutes,
  output [7:0] Heures,
  output Buzzer
);

  wire and_1_out, and_2_out, and_3_out, and_4_out;
  wire [3:0] set_valeur_heures_compteur_1_output_bus_1, set_valeur_heures_compteur_1_output_bus_2;
  wire [7:0] decompteur_1_heures_out, decompteur_1_minutes_out, decompteur_1_secondes_out, set_valeur_1_nbr,
       set_valeur_2_nbr, valeur_memory_1_output_bus_1, valeur_memory_2_output_bus_1,
       valeur_memory_3_output_bus_1;

  and and_1 (and_1_out, Set_decompteur, Start_stop);
  and and_2 (and_2_out, Mode_secondes, Set_decompteur);
  and and_3 (and_3_out, Set_decompteur, Mode_minutes);
  and and_4 (and_4_out, Set_decompteur, Mode_heures);
  set_valeur set_valeur_1 (
    .Enable(and_2_out), .Encodeur(Encodeur), .Reset(Reset), .Clock(Clk_encodeur), .Nbr(set_valeur_1_nbr));
  set_valeur set_valeur_2 (
    .Enable(and_3_out), .Encodeur(Encodeur), .Reset(Reset), .Clock(Clk_encodeur), .Nbr(set_valeur_2_nbr));
  set_valeur_heures_compteur set_valeur_heures_compteur_1 (
    .Decodeur(Encodeur), .Reset_general(Reset), .Enable(and_4_out), .Clock(Clk_encodeur),
    .Reset_synchrone(1'b0), .Output_bus_1(set_valeur_heures_compteur_1_output_bus_1),
    .Output_bus_2(set_valeur_heures_compteur_1_output_bus_2));
  valeur_memory valeur_memory_1 (
    .Valeur(set_valeur_1_nbr), .Garde_memoire(and_2_out), .Clock(Clk_encodeur), .Reset(Reset),
    .Output_bus_1(valeur_memory_1_output_bus_1));
  valeur_memory valeur_memory_2 (
    .Valeur(set_valeur_2_nbr), .Garde_memoire(and_3_out), .Clock(Clk_encodeur), .Reset(Reset),
    .Output_bus_1(valeur_memory_2_output_bus_1));
  valeur_memory valeur_memory_3 (
    .Valeur({set_valeur_heures_compteur_1_output_bus_2, set_valeur_heures_compteur_1_output_bus_1}),
    .Garde_memoire(and_4_out), .Clock(Clk_encodeur), .Reset(Reset),
    .Output_bus_1(valeur_memory_3_output_bus_1));
  Multiplexer #(.width(8)) multiplexer_1 (
    .in0(valeur_memory_2_output_bus_1), .in1(decompteur_1_minutes_out), .out(Minutes), .sel(and_1_out));
  Multiplexer #(.width(8)) multiplexer_2 (
    .in0(valeur_memory_1_output_bus_1), .in1(decompteur_1_secondes_out), .out(Secondes), .sel(and_1_out));
  Multiplexer #(.width(8)) multiplexer_3 (
    .in0(valeur_memory_3_output_bus_1), .in1(decompteur_1_heures_out), .out(Heures), .sel(and_1_out));
  decompteur decompteur_1 (
    .Clock(Clock), .Secondes(valeur_memory_1_output_bus_1), .Minutes(valeur_memory_2_output_bus_1),
    .Heures(valeur_memory_3_output_bus_1), .Fonction_enable(and_1_out), .Stop_alarme(Stop_alarme),
    .load(Function_initiate), .Reset(Reset), .Clock_bouton(Clk_encodeur),
    .Secondes_out(decompteur_1_secondes_out), .Minutes_out(decompteur_1_minutes_out),
    .Heures_out(decompteur_1_heures_out), .Buzzer(Buzzer));
endmodule

module message_musique (
  input  Enable,
  input  [1:0] Enable_message,
  input  [1:0] Enable_musique,
  input  Reset,
  input  Clock_message,
  input  Clock_bouton,
  input  Clock_musique,
  input  Re,
  input  Mi,
  input  Fa_diese,
  input  Sol,
  input  La,
  input  Si,
  input  Do,
  input  Re_haut,
  input  Do_bas,
  input  Fa,
  output [6:0] Letter_1,
  output [6:0] Letter_2,
  output [6:0] Letter_3,
  output [6:0] Letter_4,
  output [6:0] Letter_5,
  output [6:0] Letter_6,
  output Buzzer,
  output [6:0] LEDS
);

  wire demultiplexer_1_out1, demultiplexer_1_out3, demultiplexer_2_out1, demultiplexer_2_out3,
       musique_1_1_buzzer, musique_2_1_buzzer;
  wire [6:0] message_1_1_letter_1, message_1_1_letter_2, message_1_1_letter_3, message_1_1_letter_4,
       message_1_1_letter_5, message_1_1_letter_6, message_2_1_letter_1, message_2_1_letter_2,
       message_2_1_letter_3, message_2_1_letter_4, message_2_1_letter_5, message_2_1_letter_6,
       musique_1_1_led_1, musique_2_1_led_1;

  Demultiplexer #(.enable("true"), .select(2)) demultiplexer_1 (
    .out1(demultiplexer_1_out1), .out3(demultiplexer_1_out3), .in(Enable), .sel(Enable_message), .en(1'b1));  // open: out0, out2
  Demultiplexer #(.enable("true"), .select(2)) demultiplexer_2 (
    .out1(demultiplexer_2_out1), .out3(demultiplexer_2_out3), .in(Enable), .sel(Enable_musique), .en(1'b1));  // open: out0, out2
  message_1 message_1_1 (
    .Enable(demultiplexer_1_out1), .Reset(Reset), .Clock_bouton(Clock_bouton), .Clock_message(Clock_message),
    .Letter_1(message_1_1_letter_1), .Letter_2(message_1_1_letter_2), .Letter_3(message_1_1_letter_3),
    .Letter_4(message_1_1_letter_4), .Letter_5(message_1_1_letter_5), .Letter_6(message_1_1_letter_6));
  message_2 message_2_1 (
    .Enable(demultiplexer_1_out3), .Reset(Reset), .Clock_bouton(Clock_bouton), .Clock_message(Clock_message),
    .Letter_1(message_2_1_letter_1), .Letter_2(message_2_1_letter_2), .Letter_3(message_2_1_letter_3),
    .Letter_4(message_2_1_letter_4), .Letter_5(message_2_1_letter_5), .Letter_6(message_2_1_letter_6));
  musique_1 musique_1_1 (
    .Enable(demultiplexer_2_out1), .Reset(Reset), .Re(Re), .Mi(Mi), .Fa_diese(Fa_diese), .Sol(Sol), .La(La),
    .Si(Si), .Do(Do), .Re_haut(Re_haut), .Clock_musique(Clock_musique), .Buzzer(musique_1_1_buzzer),
    .LED_1(musique_1_1_led_1[0]), .LED_2(musique_1_1_led_1[1]), .LED_3(musique_1_1_led_1[2]),
    .LED_4(musique_1_1_led_1[3]), .LED_5(musique_1_1_led_1[4]), .LED_6(musique_1_1_led_1[5]),
    .LED_7(musique_1_1_led_1[6]));
  musique_2 musique_2_1 (
    .Enable(demultiplexer_2_out3), .Reset(Reset), .Re(Re), .Mi(Mi), .Fa(Fa), .Sol(Sol), .La(La), .Si(Si),
    .Do(Do), .Re_haut(Re_haut), .Do_bas(Do_bas), .Clock_musique(Clock_musique), .Buzzer(musique_2_1_buzzer),
    .LED_1(musique_2_1_led_1[0]), .LED_2(musique_2_1_led_1[1]), .LED_3(musique_2_1_led_1[2]),
    .LED_4(musique_2_1_led_1[3]), .LED_5(musique_2_1_led_1[4]), .LED_6(musique_2_1_led_1[5]),
    .LED_7(musique_2_1_led_1[6]));
  Multiplexer #(.width(7)) multiplexer_1 (
    .in0(message_1_1_letter_1), .in1(message_2_1_letter_1), .out(Letter_1), .sel(demultiplexer_1_out3));
  Multiplexer #(.width(7)) multiplexer_2 (
    .in0(message_1_1_letter_2), .in1(message_2_1_letter_2), .out(Letter_2), .sel(demultiplexer_1_out3));
  Multiplexer #(.width(7)) multiplexer_3 (
    .in0(message_1_1_letter_3), .in1(message_2_1_letter_3), .out(Letter_3), .sel(demultiplexer_1_out3));
  Multiplexer #(.width(7)) multiplexer_4 (
    .in0(message_1_1_letter_4), .in1(message_2_1_letter_4), .out(Letter_4), .sel(demultiplexer_1_out3));
  Multiplexer #(.width(7)) multiplexer_5 (
    .in0(message_1_1_letter_5), .in1(message_2_1_letter_5), .out(Letter_5), .sel(demultiplexer_1_out3));
  Multiplexer #(.width(7)) multiplexer_6 (
    .in0(message_1_1_letter_6), .in1(message_2_1_letter_6), .out(Letter_6), .sel(demultiplexer_1_out3));
  or or_1 (Buzzer, musique_1_1_buzzer, musique_2_1_buzzer);
  assign LEDS = musique_1_1_led_1 | musique_2_1_led_1;  // OR_Gate or_2, 7 bits wide
endmodule

module jeu (
  input  Enable,
  input  Start,
  input  Input_1,
  input  Input_2,
  input  Input_3,
  input  Input_4,
  input  Input_5,
  input  Input_6,
  input  Input_7,
  input  Do,
  input  Sol,
  input  La,
  input  Si,
  input  Reset,
  input  Clock_musique_jeu,
  input  Clock_jeu,
  output LED_1,
  output LED_2,
  output LED_3,
  output LED_4,
  output LED_5,
  output LED_6,
  output LED_7,
  output [6:0] s,
  output [6:0] u,
  output [6:0] c,
  output [6:0] e,
  output Buzzer
);

  wire and_1_out, and_2_out, and_3_out, and_4_out, and_5_out, and_6_out, and_7_out, and_8_out, and_9_out,
       and_10_out, compteur_1_show, not_1_out, or_2_out, score_1_result;
  wire [0:0] or_1_out;
  wire [1:0] counter_2_q;
  wire [2:0] ROM_1_data;
  wire [6:0] random_1_out;
  wire [7:0] counter_1_q;

  and and_1 (and_1_out, Enable, Start, not_1_out);
  Random #(.width(7)) random_1 (.clr(Reset), .next(and_1_out), .clk(Clock_jeu), .out(random_1_out));
  or or_1 (or_1_out[0], Input_1, Input_2, Input_3, Input_4, Input_5, Input_6, Input_7);
  not not_1 (not_1_out, or_1_out[0]);
  Counter #(.max('he)) counter_1 (
    .clr(Reset), .load(not_1_out), .up(1'b1), .count(or_2_out), .clk(Clock_musique_jeu), .D({8{1'b0}}),
    .Q(counter_1_q));  // open: carry
  compteur_jeu compteur_1 (.Start(and_1_out), .Clock(Clock_jeu), .Reset(Reset), .Show(compteur_1_show));
  score score_1 (
    .Answer_0(random_1_out[0]), .Answer_1(random_1_out[1]), .Answer_2(random_1_out[2]),
    .Answer_3(random_1_out[3]), .Answer_4(random_1_out[4]), .Answer_5(random_1_out[5]),
    .Answer_6(random_1_out[6]), .Input_0(Input_1), .Input_1(Input_2), .Input_2(Input_3), .Input_3(Input_4),
    .Input_4(Input_5), .Input_5(Input_6), .Input_6(Input_7), .Result(score_1_result));
  and and_2 (and_2_out, compteur_1_show, random_1_out[0]);
  and and_3 (and_3_out, compteur_1_show, random_1_out[1]);
  and and_4 (and_4_out, compteur_1_show, random_1_out[2]);
  and and_5 (and_5_out, compteur_1_show, random_1_out[3]);
  and and_6 (and_6_out, compteur_1_show, random_1_out[4]);
  and and_7 (and_7_out, compteur_1_show, random_1_out[5]);
  and and_8 (and_8_out, compteur_1_show, random_1_out[6]);
  and and_9 (and_9_out, or_1_out[0], score_1_result);
  and and_10 (and_10_out, or_2_out, Clock_musique_jeu);
  Counter #(.max('h1), .width(2)) counter_2 (
    .load(and_9_out), .D({1'b0, or_1_out[0]}), .count(and_9_out), .Q(counter_2_q), .up(1'b1),
    .clk(Clock_jeu), .clr(not_1_out));  // open: carry
  or or_2 (or_2_out, counter_2_q[0], counter_2_q[1]);
  ROM #(.dataWidth(3)) ROM_1 (.addr(counter_1_q), .data(ROM_1_data));
  or or_3 (LED_1, and_2_out, and_10_out);
  or or_4 (LED_2, and_3_out, and_10_out);
  or or_5 (LED_3, and_4_out, and_10_out);
  or or_6 (LED_4, and_5_out, and_10_out);
  or or_7 (LED_5, and_6_out, and_10_out);
  or or_8 (LED_6, and_7_out, and_10_out);
  or or_9 (LED_7, and_8_out, and_10_out);
  Multiplexer #(.select(3)) multiplexer_1 (
    .in0(1'b0), .in1(Do), .in2(Sol), .in3(La), .in4(Si), .in5(1'b0), .in6(1'b0), .in7(1'b0), .out(Buzzer),
    .sel(ROM_1_data));
  succes succes_1 (
    .Enable(or_2_out), .s_a(s[0]), .s_b(s[1]), .s_c(s[2]), .s_d(s[3]), .s_e(s[4]), .s_f(s[5]), .s_g(s[6]),
    .u_a(u[0]), .u_b(u[1]), .u_c(u[2]), .u_d(u[3]), .u_e(u[4]), .u_f(u[5]), .u_g(u[6]), .c_a(c[0]),
    .c_b(c[1]), .c_c(c[2]), .c_d(c[3]), .c_e(c[4]), .c_f(c[5]), .c_g(c[6]), .e_a(e[0]), .e_b(e[1]),
    .e_c(e[2]), .e_d(e[3]), .e_e(e[4]), .e_f(e[5]), .e_g(e[6]));

  // Notes on the sheet:
  //   contents of ROM_1 (hex, n*v repeats v):
  //   0 0 1 1 0 2 3 3 2 2 0 0 4 4 1 1
endmodule

module number (
  input  [3:0] nbr,
  output a_out,
  output b_out,
  output c_out,
  output d_out,
  output e_out,
  output f_out,
  output g_out
);

  a a_1 (.W(nbr[3]), .X(nbr[2]), .Y(nbr[1]), .Z(nbr[0]), .a_output(a_out));
  b b_1 (.W(nbr[3]), .X(nbr[2]), .Y(nbr[1]), .Z(nbr[0]), .b_output(b_out));
  c c_1 (.W(nbr[3]), .X(nbr[2]), .Y(nbr[1]), .Z(nbr[0]), .c_output(c_out));
  d d_1 (.W(nbr[3]), .X(nbr[2]), .Y(nbr[1]), .Z(nbr[0]), .d_output(d_out));
  e e_1 (.W(nbr[3]), .X(nbr[2]), .Y(nbr[1]), .Z(nbr[0]), .e_output(e_out));
  f f_1 (.W(nbr[3]), .X(nbr[2]), .Y(nbr[1]), .Z(nbr[0]), .f_output(f_out));
  g g_1 (.W(nbr[3]), .X(nbr[2]), .Y(nbr[1]), .Z(nbr[0]), .g_output(g_out));
endmodule

module compteur_complet (
  input  CH_C,
  input  [1:0] Encodeur,
  input  Clock_bouton,
  input  Reset,
  input  Clk_encodeur,
  output Set_alarme,
  output Set_chrono,
  output Set_decompteur,
  output Set_song,
  output Set_jeu,
  output [3:0] Affichage_menu,
  output Mode_sec,
  output Mode_min,
  output Mode_heure,
  output Fct_enable,
  output Mode_menu
);

  wire and_1_out, and_2_out, chanel_c_set_1_set_alarme, chanel_c_set_1_set_chrono,
       chanel_c_set_1_set_decompteur, chanel_c_set_1_set_jeu, chanel_c_set_1_set_song,
       compteur_chanel_c_1_reset, or_1_out;
  wire [1:0] counter_1_q;

  compteur_chanel_c compteur_chanel_c_1 (
    .CH_C(CH_C), .Clock(Clock_bouton), .Chrono_selected(and_2_out), .Reset_input(Reset),
    .Mode_menu(Mode_menu), .Ajuster_sec(Mode_sec), .Ajuster_min(Mode_min), .Ajuster_heures(Mode_heure),
    .Fonction_enable(Fct_enable), .Reset(compteur_chanel_c_1_reset));
  and and_1 (and_1_out, Mode_menu, CH_C);
  Counter #(.max('h1), .width(2)) counter_1 (
    .clr(Reset), .load(compteur_chanel_c_1_reset), .up(1'b1), .count(and_1_out), .clk(Clock_bouton),
    .D(2'b00), .Q(counter_1_q));  // open: carry
  chanel_c_set chanel_c_set_1 (
    .CH_C_set_mode(Mode_menu), .Encodeur(Encodeur), .Reset(compteur_chanel_c_1_reset), .Clock(Clk_encodeur),
    .Reset_general(Reset), .Set_alarme(chanel_c_set_1_set_alarme), .Set_chrono(chanel_c_set_1_set_chrono),
    .Set_decompteur(chanel_c_set_1_set_decompteur), .Set_song(chanel_c_set_1_set_song),
    .Set_jeu(chanel_c_set_1_set_jeu), .Affichage_menu_0(Affichage_menu[0]),
    .Affichage_menu_1(Affichage_menu[1]), .Affichage_menu_2(Affichage_menu[2]),
    .Affichage_menu_3(Affichage_menu[3]));
  and and_2 (and_2_out, Set_chrono, ~Mode_menu);  // AND_Gate
  or or_1 (or_1_out, counter_1_q[0], counter_1_q[1]);
  and and_3 (Set_alarme, chanel_c_set_1_set_alarme, or_1_out);
  and and_4 (Set_chrono, chanel_c_set_1_set_chrono, or_1_out);
  and and_5 (Set_decompteur, chanel_c_set_1_set_decompteur, or_1_out);
  and and_6 (Set_song, chanel_c_set_1_set_song, or_1_out);
  and and_7 (Set_jeu, chanel_c_set_1_set_jeu, or_1_out);

  // Other names for the same wires on the sheet: ajuster_heure = Mode_heure; ajuster_min = Mode_min;
  //   ajuster_sec = Mode_sec; clk_bouton = Clock_bouton; fonction_enable = Fct_enable
endmodule

module additioneur (
  input  A0,
  input  B0,
  input  A1,
  input  B1,
  input  A2,
  input  B2,
  input  A3,
  input  B3,
  input  carry_in,
  output Y0,
  output Y1,
  output Y2,
  output Y3,
  output Carry_out
);

  wire and_1_out, and_6_out, Y_0_1_c0, Y_0_1_y0_output, Y_i_1_c_i_output, Y_i_1_y_i_output, Y_i_2_c_i_output,
       Y_i_2_y_i_output, Y_i_3_c_i_output, Y_i_3_y_i_output;

  Y_0 Y_0_1 (.A0(A0), .B0(B0), .Carry(carry_in), .Y0_output(Y_0_1_y0_output), .C0(Y_0_1_c0));
  Y_i Y_i_1 (.A_i(A1), .B_i(B1), .C_i(Y_0_1_c0), .Y_i_output(Y_i_1_y_i_output), .C_i_output(Y_i_1_c_i_output));
  Y_i Y_i_2 (.A_i(A2), .B_i(B2), .C_i(Y_i_1_c_i_output), .Y_i_output(Y_i_2_y_i_output), .C_i_output(Y_i_2_c_i_output));
  Y_i Y_i_3 (.A_i(A3), .B_i(B3), .C_i(Y_i_2_c_i_output), .Y_i_output(Y_i_3_y_i_output), .C_i_output(Y_i_3_c_i_output));
  and and_1 (and_1_out, Y_i_3_y_i_output, Y_i_1_y_i_output);
  and and_2 (Y0, Y_0_1_y0_output, ~and_1_out);  // AND_Gate
  and and_3 (Y1, Y_i_1_y_i_output, ~and_1_out);  // AND_Gate
  and and_4 (Y2, Y_i_2_y_i_output, ~and_1_out);  // AND_Gate
  and and_5 (Y3, Y_i_3_y_i_output, ~and_1_out);  // AND_Gate
  and and_6 (and_6_out, Y_i_3_c_i_output, ~and_1_out);  // AND_Gate
  or or_1 (Carry_out, and_6_out, and_1_out);
endmodule

module alarme (
  input  Alarme_on,
  input  [7:0] secondes,
  input  [7:0] secondes_reel,
  input  [7:0] minutes,
  input  [7:0] minutes_reel,
  input  [7:0] heures,
  input  [7:0] heures_real,
  input  clock,
  input  Reset,
  output Buzzer
);

  wire nor_1_out, not_1_out, or_1_out, xor_1_out, xor_2_out, xor_3_out, xor_4_out, xor_5_out, xor_6_out,
       xor_7_out, xor_8_out, xor_9_out, xor_10_out, xor_11_out, xor_12_out, xor_13_out, xor_14_out,
       xor_15_out, xor_16_out, xor_17_out, xor_18_out, xor_19_out, xor_20_out, xor_21_out, xor_22_out,
       xor_23_out, xor_24_out;
  wire [1:0] counter_1_q;

  not not_1 (not_1_out, Alarme_on);
  xor xor_1 (xor_1_out, secondes[0], secondes_reel[0]);
  xor xor_2 (xor_2_out, secondes[1], secondes_reel[1]);
  xor xor_3 (xor_3_out, secondes_reel[2], secondes[2]);
  xor xor_4 (xor_4_out, secondes_reel[3], secondes[3]);
  xor xor_5 (xor_5_out, secondes[4], secondes_reel[4]);
  xor xor_6 (xor_6_out, secondes[5], secondes_reel[5]);
  xor xor_7 (xor_7_out, secondes_reel[6], secondes[6]);
  xor xor_8 (xor_8_out, secondes_reel[7], secondes[7]);
  xor xor_9 (xor_9_out, minutes[0], minutes_reel[0]);
  xor xor_10 (xor_10_out, minutes[1], minutes_reel[1]);
  xor xor_11 (xor_11_out, minutes_reel[2], minutes[2]);
  xor xor_12 (xor_12_out, minutes_reel[3], minutes[3]);
  xor xor_13 (xor_13_out, minutes[4], minutes_reel[4]);
  xor xor_14 (xor_14_out, minutes[5], minutes_reel[5]);
  xor xor_15 (xor_15_out, minutes_reel[6], minutes[6]);
  xor xor_16 (xor_16_out, minutes_reel[7], minutes[7]);
  xor xor_17 (xor_17_out, heures[0], heures_real[0]);
  xor xor_18 (xor_18_out, heures[1], heures_real[1]);
  xor xor_19 (xor_19_out, heures_real[2], heures[2]);
  xor xor_20 (xor_20_out, heures_real[3], heures[3]);
  xor xor_21 (xor_21_out, heures[4], heures_real[4]);
  xor xor_22 (xor_22_out, heures[5], heures_real[5]);
  xor xor_23 (xor_23_out, heures_real[6], heures[6]);
  xor xor_24 (xor_24_out, heures_real[7], heures[7]);
  nor nor_1 (nor_1_out, not_1_out, xor_1_out, xor_2_out, xor_3_out, xor_4_out, xor_5_out, xor_6_out, xor_7_out, xor_8_out, xor_9_out, xor_10_out, xor_11_out, xor_12_out, xor_13_out, xor_14_out, xor_15_out, xor_16_out, xor_17_out, xor_18_out, xor_19_out, xor_20_out, xor_21_out, xor_22_out, xor_23_out, xor_24_out);
  Counter #(.max('h1), .width(2)) counter_1 (
    .clr(or_1_out), .load(nor_1_out), .up(nor_1_out), .count(nor_1_out), .clk(clock), .D(2'b01),
    .Q(counter_1_q));  // open: carry
  or or_1 (or_1_out, not_1_out, Reset);
  or or_2 (Buzzer, counter_1_q[0], counter_1_q[1]);
endmodule

module message_1 (
  input  Enable,
  input  Reset,
  input  Clock_bouton,
  input  Clock_message,
  output [6:0] Letter_1,
  output [6:0] Letter_2,
  output [6:0] Letter_3,
  output [6:0] Letter_4,
  output [6:0] Letter_5,
  output [6:0] Letter_6
);

  wire letter_controle_2_1_y0_output, letter_controle_2_1_y1_output, letter_controle_2_1_y2_output,
       letter_controle_2_1_y3_output, letter_controle_2_2_y0_output, letter_controle_2_2_y1_output,
       letter_controle_2_2_y2_output, letter_controle_2_2_y3_output, letter_controle_2_3_y0_output,
       letter_controle_2_3_y1_output, letter_controle_2_3_y2_output, letter_controle_2_3_y3_output,
       letter_controle_2_4_y0_output, letter_controle_2_4_y1_output, letter_controle_2_4_y2_output,
       letter_controle_2_4_y3_output, letter_controle_2_5_y0_output, letter_controle_2_5_y1_output,
       letter_controle_2_5_y2_output, letter_controle_2_5_y3_output, letter_controle_2_6_y0_output,
       letter_controle_2_6_y1_output, letter_controle_2_6_y2_output, letter_controle_2_6_y3_output;

  letter_controle letter_controle_2_1 (
    .Clock(Clock_message), .Enable(Enable), .Clock_counter(Clock_bouton), .Reset(Reset),
    .Enable_general(Enable), .Y0_output(letter_controle_2_1_y0_output),
    .Y1_output(letter_controle_2_1_y1_output), .Y2_output(letter_controle_2_1_y2_output),
    .Y3_output(letter_controle_2_1_y3_output));
  letter_controle letter_controle_2_2 (
    .Clock(Clock_message), .Enable(letter_controle_2_1_y3_output), .Clock_counter(Clock_bouton),
    .Reset(Reset), .Enable_general(Enable), .Y0_output(letter_controle_2_2_y0_output),
    .Y1_output(letter_controle_2_2_y1_output), .Y2_output(letter_controle_2_2_y2_output),
    .Y3_output(letter_controle_2_2_y3_output));
  letter_controle letter_controle_2_3 (
    .Clock(Clock_message), .Enable(letter_controle_2_2_y3_output), .Clock_counter(Clock_bouton),
    .Reset(Reset), .Enable_general(Enable), .Y0_output(letter_controle_2_3_y0_output),
    .Y1_output(letter_controle_2_3_y1_output), .Y2_output(letter_controle_2_3_y2_output),
    .Y3_output(letter_controle_2_3_y3_output));
  letter_controle letter_controle_2_4 (
    .Clock(Clock_message), .Enable(letter_controle_2_3_y3_output), .Clock_counter(Clock_bouton),
    .Reset(Reset), .Enable_general(Enable), .Y0_output(letter_controle_2_4_y0_output),
    .Y1_output(letter_controle_2_4_y1_output), .Y2_output(letter_controle_2_4_y2_output),
    .Y3_output(letter_controle_2_4_y3_output));
  letter_controle letter_controle_2_5 (
    .Clock(Clock_message), .Enable(letter_controle_2_4_y3_output), .Clock_counter(Clock_bouton),
    .Reset(Reset), .Enable_general(Enable), .Y0_output(letter_controle_2_5_y0_output),
    .Y1_output(letter_controle_2_5_y1_output), .Y2_output(letter_controle_2_5_y2_output),
    .Y3_output(letter_controle_2_5_y3_output));
  letter_controle letter_controle_2_6 (
    .Clock(Clock_message), .Enable(letter_controle_2_5_y3_output), .Clock_counter(Clock_bouton),
    .Reset(Reset), .Enable_general(Enable), .Y0_output(letter_controle_2_6_y0_output),
    .Y1_output(letter_controle_2_6_y1_output), .Y2_output(letter_controle_2_6_y2_output),
    .Y3_output(letter_controle_2_6_y3_output));
  letter_affichage letter_affichage_1 (
    .Y_0(letter_controle_2_1_y0_output), .Y_1(letter_controle_2_1_y1_output),
    .Y_2(letter_controle_2_1_y2_output), .Y_3(letter_controle_2_1_y3_output), .a(Letter_1[0]),
    .b(Letter_1[1]), .c(Letter_1[2]), .d(Letter_1[3]), .e(Letter_1[4]), .f(Letter_1[5]), .g(Letter_1[6]));
  letter_affichage letter_affichage_2 (
    .Y_0(letter_controle_2_2_y0_output), .Y_1(letter_controle_2_2_y1_output),
    .Y_2(letter_controle_2_2_y2_output), .Y_3(letter_controle_2_2_y3_output), .a(Letter_2[0]),
    .b(Letter_2[1]), .c(Letter_2[2]), .d(Letter_2[3]), .e(Letter_2[4]), .f(Letter_2[5]), .g(Letter_2[6]));
  letter_affichage letter_affichage_3 (
    .Y_0(letter_controle_2_3_y0_output), .Y_1(letter_controle_2_3_y1_output),
    .Y_2(letter_controle_2_3_y2_output), .Y_3(letter_controle_2_3_y3_output), .a(Letter_3[0]),
    .b(Letter_3[1]), .c(Letter_3[2]), .d(Letter_3[3]), .e(Letter_3[4]), .f(Letter_3[5]), .g(Letter_3[6]));
  letter_affichage letter_affichage_4 (
    .Y_0(letter_controle_2_4_y0_output), .Y_1(letter_controle_2_4_y1_output),
    .Y_2(letter_controle_2_4_y2_output), .Y_3(letter_controle_2_4_y3_output), .a(Letter_4[0]),
    .b(Letter_4[1]), .c(Letter_4[2]), .d(Letter_4[3]), .e(Letter_4[4]), .f(Letter_4[5]), .g(Letter_4[6]));
  letter_affichage letter_affichage_5 (
    .Y_0(letter_controle_2_5_y0_output), .Y_1(letter_controle_2_5_y1_output),
    .Y_2(letter_controle_2_5_y2_output), .Y_3(letter_controle_2_5_y3_output), .a(Letter_5[0]),
    .b(Letter_5[1]), .c(Letter_5[2]), .d(Letter_5[3]), .e(Letter_5[4]), .f(Letter_5[5]), .g(Letter_5[6]));
  letter_affichage letter_affichage_6 (
    .Y_0(letter_controle_2_6_y0_output), .Y_1(letter_controle_2_6_y1_output),
    .Y_2(letter_controle_2_6_y2_output), .Y_3(letter_controle_2_6_y3_output), .a(Letter_6[0]),
    .b(Letter_6[1]), .c(Letter_6[2]), .d(Letter_6[3]), .e(Letter_6[4]), .f(Letter_6[5]), .g(Letter_6[6]));
endmodule

module message_2 (
  input  Enable,
  input  Reset,
  input  Clock_bouton,
  input  Clock_message,
  output [6:0] Letter_1,
  output [6:0] Letter_2,
  output [6:0] Letter_3,
  output [6:0] Letter_4,
  output [6:0] Letter_5,
  output [6:0] Letter_6
);

  wire letter_controle_2_1_y0_output, letter_controle_2_1_y1_output, letter_controle_2_1_y2_output,
       letter_controle_2_1_y3_output, letter_controle_2_2_y0_output, letter_controle_2_2_y1_output,
       letter_controle_2_2_y2_output, letter_controle_2_2_y3_output, letter_controle_2_3_y0_output,
       letter_controle_2_3_y1_output, letter_controle_2_3_y2_output, letter_controle_2_3_y3_output,
       letter_controle_2_4_y0_output, letter_controle_2_4_y1_output, letter_controle_2_4_y2_output,
       letter_controle_2_4_y3_output, letter_controle_2_5_y0_output, letter_controle_2_5_y1_output,
       letter_controle_2_5_y2_output, letter_controle_2_5_y3_output, letter_controle_2_6_y0_output,
       letter_controle_2_6_y1_output, letter_controle_2_6_y2_output, letter_controle_2_6_y3_output;

  letter_controle_2 letter_controle_2_1 (
    .Clock(Clock_message), .Enable(Enable), .Clock_counter(Clock_bouton), .Reset(Reset),
    .Enable_general(Enable), .Y0_output(letter_controle_2_1_y0_output),
    .Y1_output(letter_controle_2_1_y1_output), .Y2_output(letter_controle_2_1_y2_output),
    .Y3_output(letter_controle_2_1_y3_output));
  letter_controle_2 letter_controle_2_2 (
    .Clock(Clock_message), .Enable(letter_controle_2_1_y3_output), .Clock_counter(Clock_bouton),
    .Reset(Reset), .Enable_general(Enable), .Y0_output(letter_controle_2_2_y0_output),
    .Y1_output(letter_controle_2_2_y1_output), .Y2_output(letter_controle_2_2_y2_output),
    .Y3_output(letter_controle_2_2_y3_output));
  letter_controle_2 letter_controle_2_3 (
    .Clock(Clock_message), .Enable(letter_controle_2_2_y3_output), .Clock_counter(Clock_bouton),
    .Reset(Reset), .Enable_general(Enable), .Y0_output(letter_controle_2_3_y0_output),
    .Y1_output(letter_controle_2_3_y1_output), .Y2_output(letter_controle_2_3_y2_output),
    .Y3_output(letter_controle_2_3_y3_output));
  letter_controle_2 letter_controle_2_4 (
    .Clock(Clock_message), .Enable(letter_controle_2_3_y3_output), .Clock_counter(Clock_bouton),
    .Reset(Reset), .Enable_general(Enable), .Y0_output(letter_controle_2_4_y0_output),
    .Y1_output(letter_controle_2_4_y1_output), .Y2_output(letter_controle_2_4_y2_output),
    .Y3_output(letter_controle_2_4_y3_output));
  letter_controle_2 letter_controle_2_5 (
    .Clock(Clock_message), .Enable(letter_controle_2_4_y3_output), .Clock_counter(Clock_bouton),
    .Reset(Reset), .Enable_general(Enable), .Y0_output(letter_controle_2_5_y0_output),
    .Y1_output(letter_controle_2_5_y1_output), .Y2_output(letter_controle_2_5_y2_output),
    .Y3_output(letter_controle_2_5_y3_output));
  letter_controle_2 letter_controle_2_6 (
    .Clock(Clock_message), .Enable(letter_controle_2_5_y3_output), .Clock_counter(Clock_bouton),
    .Reset(Reset), .Enable_general(Enable), .Y0_output(letter_controle_2_6_y0_output),
    .Y1_output(letter_controle_2_6_y1_output), .Y2_output(letter_controle_2_6_y2_output),
    .Y3_output(letter_controle_2_6_y3_output));
  letter_affichage_2 letter_affichage_2_1 (
    .Y_0(letter_controle_2_1_y0_output), .Y_1(letter_controle_2_1_y1_output),
    .Y_2(letter_controle_2_1_y2_output), .Y_3(letter_controle_2_1_y3_output), .a(Letter_1[0]),
    .b(Letter_1[1]), .c(Letter_1[2]), .d(Letter_1[3]), .e(Letter_1[4]), .f(Letter_1[5]), .g(Letter_1[6]));
  letter_affichage_2 letter_affichage_2_2 (
    .Y_0(letter_controle_2_2_y0_output), .Y_1(letter_controle_2_2_y1_output),
    .Y_2(letter_controle_2_2_y2_output), .Y_3(letter_controle_2_2_y3_output), .a(Letter_2[0]),
    .b(Letter_2[1]), .c(Letter_2[2]), .d(Letter_2[3]), .e(Letter_2[4]), .f(Letter_2[5]), .g(Letter_2[6]));
  letter_affichage_2 letter_affichage_2_3 (
    .Y_0(letter_controle_2_3_y0_output), .Y_1(letter_controle_2_3_y1_output),
    .Y_2(letter_controle_2_3_y2_output), .Y_3(letter_controle_2_3_y3_output), .a(Letter_3[0]),
    .b(Letter_3[1]), .c(Letter_3[2]), .d(Letter_3[3]), .e(Letter_3[4]), .f(Letter_3[5]), .g(Letter_3[6]));
  letter_affichage_2 letter_affichage_2_4 (
    .Y_0(letter_controle_2_4_y0_output), .Y_1(letter_controle_2_4_y1_output),
    .Y_2(letter_controle_2_4_y2_output), .Y_3(letter_controle_2_4_y3_output), .a(Letter_4[0]),
    .b(Letter_4[1]), .c(Letter_4[2]), .d(Letter_4[3]), .e(Letter_4[4]), .f(Letter_4[5]), .g(Letter_4[6]));
  letter_affichage_2 letter_affichage_2_5 (
    .Y_0(letter_controle_2_5_y0_output), .Y_1(letter_controle_2_5_y1_output),
    .Y_2(letter_controle_2_5_y2_output), .Y_3(letter_controle_2_5_y3_output), .a(Letter_5[0]),
    .b(Letter_5[1]), .c(Letter_5[2]), .d(Letter_5[3]), .e(Letter_5[4]), .f(Letter_5[5]), .g(Letter_5[6]));
  letter_affichage_2 letter_affichage_2_6 (
    .Y_0(letter_controle_2_6_y0_output), .Y_1(letter_controle_2_6_y1_output),
    .Y_2(letter_controle_2_6_y2_output), .Y_3(letter_controle_2_6_y3_output), .a(Letter_6[0]),
    .b(Letter_6[1]), .c(Letter_6[2]), .d(Letter_6[3]), .e(Letter_6[4]), .f(Letter_6[5]), .g(Letter_6[6]));
endmodule

module musique_1 (
  input  Enable,
  input  Reset,
  input  Re,
  input  Mi,
  input  Fa_diese,
  input  Sol,
  input  La,
  input  Si,
  input  Do,
  input  Re_haut,
  input  Clock_musique,
  output Buzzer,
  output LED_1,
  output LED_2,
  output LED_3,
  output LED_4,
  output LED_5,
  output LED_6,
  output LED_7
);

  wire demultiplexer_1_out1, demultiplexer_1_out8, multiplexer_1_out, not_1_out;
  wire [3:0] ROM_1_data;
  wire [7:0] counter_1_q;

  not not_1 (not_1_out, Enable);
  Counter #(.max('ha0)) counter_1 (
    .clr(Reset), .load(not_1_out), .up(1'b1), .count(Enable), .clk(Clock_musique), .D({8{1'b0}}),
    .Q(counter_1_q));  // open: carry
  ROM #(.dataWidth(4)) ROM_1 (.addr(counter_1_q), .data(ROM_1_data));
  Multiplexer #(.select(4)) multiplexer_1 (
    .in0(1'b0), .in1(Re), .in2(Mi), .in3(Fa_diese), .in4(Sol), .in5(La), .in6(Si), .in7(Do), .in8(Re_haut),
    .in9(1'b0), .in10(1'b0), .in11(1'b0), .in12(1'b0), .in13(1'b0), .in14(1'b0), .in15(1'b0),
    .out(multiplexer_1_out), .sel(ROM_1_data));
  and and_1 (Buzzer, Enable, multiplexer_1_out);
  Demultiplexer #(.enable("true"), .select(4)) demultiplexer_1 (
    .out1(demultiplexer_1_out1), .out2(LED_2), .out3(LED_3), .out4(LED_4), .out5(LED_5), .out6(LED_6),
    .out7(LED_7), .out8(demultiplexer_1_out8), .in(1'b1), .sel(ROM_1_data), .en(1'b1));  // open: out0, out9, out10, out11, out12, out13, out14, out15
  or or_1 (LED_1, demultiplexer_1_out8, demultiplexer_1_out1);

  // Notes on the sheet:
  //   contents of ROM_1 (hex, n*v repeats v):
  //   0 0 4*4 0 0 1 1 4*4 0 0 1 1 4 4 1 1 4 4 6 6 4*8 4*0 4*7 0 0 5 5 4*7 0 0 5 5 7 7 5 5 3 3 5 5 4*1 4*0
  //   4 4 0 0 6*4 6 6 5 5 4*4 8*3 5 5 7 7 3 3 5 5 8*4 6 6 5 5 4*4 8*3 5 5 7 7 3 3 4 0 4 0 4 3 2 3 4 0 4 0
  //   6 5 4 5 6 0 6 0 8 7 6 7 8 8
endmodule

module musique_2 (
  input  Enable,
  input  Reset,
  input  Re,
  input  Mi,
  input  Fa,
  input  Sol,
  input  La,
  input  Si,
  input  Do,
  input  Re_haut,
  input  Do_bas,
  input  Clock_musique,
  output Buzzer,
  output LED_1,
  output LED_2,
  output LED_3,
  output LED_4,
  output LED_5,
  output LED_6,
  output LED_7
);

  wire demultiplexer_1_out1, demultiplexer_1_out6, demultiplexer_1_out8, demultiplexer_1_out9,
       multiplexer_1_out, not_1_out;
  wire [3:0] ROM_1_data;
  wire [7:0] counter_1_q;

  not not_1 (not_1_out, Enable);
  Counter #(.max('h90)) counter_1 (
    .clr(Reset), .load(not_1_out), .up(1'b1), .count(Enable), .clk(Clock_musique), .D({8{1'b0}}),
    .Q(counter_1_q));  // open: carry
  ROM #(.dataWidth(4)) ROM_1 (.addr(counter_1_q), .data(ROM_1_data));
  Multiplexer #(.select(4)) multiplexer_1 (
    .in0(1'b0), .in1(Re), .in2(Mi), .in3(Fa), .in4(Sol), .in5(La), .in6(Si), .in7(Do), .in8(Re_haut),
    .in9(Do_bas), .in10(1'b0), .in11(1'b0), .in12(1'b0), .in13(1'b0), .in14(1'b0), .in15(1'b0),
    .out(multiplexer_1_out), .sel(ROM_1_data));
  Demultiplexer #(.enable("true"), .select(4)) demultiplexer_1 (
    .out1(demultiplexer_1_out1), .out2(LED_2), .out3(LED_3), .out4(LED_4), .out5(LED_5),
    .out6(demultiplexer_1_out6), .out7(LED_7), .out8(demultiplexer_1_out8), .out9(demultiplexer_1_out9),
    .in(1'b1), .sel(ROM_1_data), .en(1'b1));  // open: out0, out10, out11, out12, out13, out14, out15
  and and_1 (Buzzer, Enable, multiplexer_1_out);
  or or_1 (LED_1, demultiplexer_1_out8, demultiplexer_1_out1);
  or or_2 (LED_6, demultiplexer_1_out6, demultiplexer_1_out9);

  // Notes on the sheet:
  //   contents of ROM_1 (hex, n*v repeats v):
  //   4*0 4*2 4*0 4*2 4*0 12*2 4*4 4*3 4*1 4*3 4*5 6*4 2 2 4*4 4*0 4*7 4 4 0 0 4*4 2 2 0 0 4*1 4*5 4 4 3 3
  //   2 2 1 1 8*9 2 2 1 1 9 9 1 1 4*9
endmodule

module set_valeur (
  input  Enable,
  input  [1:0] Encodeur,
  input  Reset,
  input  Clock,
  output [7:0] Nbr
);

  wire and_1_out, and_2_out, and_3_out, and_4_out, and_5_out, and_6_out, and_7_out, and_8_out, and_9_out,
       and_10_out, and_11_out, and_12_out, and_13_out, and_14_out, and_15_out, and_16_out, d_ff_1_q,
       d_ff_2_q, d_ff_3_q, d_ff_4_q, d_ff_5_q, d_ff_6_q, d_ff_7_q, d_ff_8_q;
  wire [3:0] compteur_59_1_output_bus_1, compteur_59_1_output_bus_2;

  compteur_59 compteur_59_1 (
    .CH_A(Encodeur[0]), .CH_B(Encodeur[1]), .Reset_general(Reset), .Enable(Enable), .Clock(Clock),
    .Reset_synchrone(1'b0), .Output_bus_1(compteur_59_1_output_bus_1),
    .Output_bus_2(compteur_59_1_output_bus_2));
  D_Flip_Flop d_ff_1 (.D(d_ff_1_q), .clk(Clock), .Q(d_ff_1_q), .preset(1'b0), .reset(Reset));  // open: Qn
  D_Flip_Flop d_ff_2 (.D(d_ff_2_q), .clk(Clock), .Q(d_ff_2_q), .preset(1'b0), .reset(Reset));  // open: Qn
  D_Flip_Flop d_ff_3 (.D(d_ff_3_q), .clk(Clock), .Q(d_ff_3_q), .preset(1'b0), .reset(Reset));  // open: Qn
  D_Flip_Flop d_ff_4 (.D(d_ff_4_q), .clk(Clock), .Q(d_ff_4_q), .preset(1'b0), .reset(Reset));  // open: Qn
  D_Flip_Flop d_ff_5 (.D(d_ff_5_q), .clk(Clock), .Q(d_ff_5_q), .preset(1'b0), .reset(Reset));  // open: Qn
  D_Flip_Flop d_ff_6 (.D(d_ff_6_q), .clk(Clock), .Q(d_ff_6_q), .preset(1'b0), .reset(Reset));  // open: Qn
  D_Flip_Flop d_ff_7 (.D(d_ff_7_q), .clk(Clock), .Q(d_ff_7_q), .preset(1'b0), .reset(Reset));  // open: Qn
  D_Flip_Flop d_ff_8 (.D(d_ff_8_q), .clk(Clock), .Q(d_ff_8_q), .preset(1'b0), .reset(Reset));  // open: Qn
  and and_1 (and_1_out, d_ff_1_q, ~Enable);  // AND_Gate
  and and_2 (and_2_out, compteur_59_1_output_bus_1[0], Enable);
  and and_3 (and_3_out, d_ff_2_q, ~Enable);  // AND_Gate
  and and_4 (and_4_out, compteur_59_1_output_bus_1[1], Enable);
  and and_5 (and_5_out, d_ff_3_q, ~Enable);  // AND_Gate
  and and_6 (and_6_out, compteur_59_1_output_bus_1[2], Enable);
  and and_7 (and_7_out, d_ff_4_q, ~Enable);  // AND_Gate
  and and_8 (and_8_out, compteur_59_1_output_bus_1[3], Enable);
  and and_9 (and_9_out, d_ff_5_q, ~Enable);  // AND_Gate
  and and_10 (and_10_out, compteur_59_1_output_bus_2[0], Enable);
  and and_11 (and_11_out, d_ff_6_q, ~Enable);  // AND_Gate
  and and_12 (and_12_out, compteur_59_1_output_bus_2[1], Enable);
  and and_13 (and_13_out, d_ff_7_q, ~Enable);  // AND_Gate
  and and_14 (and_14_out, compteur_59_1_output_bus_2[2], Enable);
  and and_15 (and_15_out, d_ff_8_q, ~Enable);  // AND_Gate
  and and_16 (and_16_out, compteur_59_1_output_bus_2[3], Enable);
  or or_1 (Nbr[0], and_1_out, and_2_out);
  or or_2 (Nbr[1], and_3_out, and_4_out);
  or or_3 (Nbr[2], and_5_out, and_6_out);
  or or_4 (Nbr[3], and_7_out, and_8_out);
  or or_5 (Nbr[4], and_9_out, and_10_out);
  or or_6 (Nbr[5], and_11_out, and_12_out);
  or or_7 (Nbr[6], and_13_out, and_14_out);
  or or_8 (Nbr[7], and_15_out, and_16_out);
endmodule

module set_valeur_heures (
  input  Enable,
  input  [1:0] Decodeur,
  input  Reset,
  input  Clock,
  output [7:0] Nbr
);

  wire and_1_out, and_2_out, and_3_out, and_4_out, and_5_out, and_6_out, and_7_out, and_8_out, and_9_out,
       and_10_out, and_11_out, and_12_out, and_13_out, and_14_out, and_15_out, and_16_out, d_ff_1_q,
       d_ff_2_q, d_ff_3_q, d_ff_4_q, d_ff_5_q, d_ff_6_q, d_ff_7_q, d_ff_8_q;
  wire [3:0] set_valeur_heures_compteur_1_output_bus_1, set_valeur_heures_compteur_1_output_bus_2;

  set_valeur_heures_compteur set_valeur_heures_compteur_1 (
    .Decodeur(Decodeur), .Reset_general(Reset), .Enable(Enable), .Clock(Clock), .Reset_synchrone(1'b0),
    .Output_bus_1(set_valeur_heures_compteur_1_output_bus_1),
    .Output_bus_2(set_valeur_heures_compteur_1_output_bus_2));
  D_Flip_Flop d_ff_1 (.D(d_ff_1_q), .clk(Clock), .Q(d_ff_1_q), .preset(1'b0), .reset(Reset));  // open: Qn
  D_Flip_Flop d_ff_2 (.D(d_ff_2_q), .clk(Clock), .Q(d_ff_2_q), .preset(1'b0), .reset(Reset));  // open: Qn
  D_Flip_Flop d_ff_3 (.D(d_ff_3_q), .clk(Clock), .Q(d_ff_3_q), .preset(1'b0), .reset(Reset));  // open: Qn
  D_Flip_Flop d_ff_4 (.D(d_ff_4_q), .clk(Clock), .Q(d_ff_4_q), .preset(1'b0), .reset(Reset));  // open: Qn
  D_Flip_Flop d_ff_5 (.D(d_ff_5_q), .clk(Clock), .Q(d_ff_5_q), .preset(1'b0), .reset(Reset));  // open: Qn
  D_Flip_Flop d_ff_6 (.D(d_ff_6_q), .clk(Clock), .Q(d_ff_6_q), .preset(1'b0), .reset(Reset));  // open: Qn
  D_Flip_Flop d_ff_7 (.D(d_ff_7_q), .clk(Clock), .Q(d_ff_7_q), .preset(1'b0), .reset(Reset));  // open: Qn
  D_Flip_Flop d_ff_8 (.D(d_ff_8_q), .clk(Clock), .Q(d_ff_8_q), .preset(1'b0), .reset(Reset));  // open: Qn
  and and_1 (and_1_out, d_ff_1_q, ~Enable);  // AND_Gate
  and and_2 (and_2_out, set_valeur_heures_compteur_1_output_bus_1[0], Enable);
  and and_3 (and_3_out, d_ff_2_q, ~Enable);  // AND_Gate
  and and_4 (and_4_out, set_valeur_heures_compteur_1_output_bus_1[1], Enable);
  and and_5 (and_5_out, d_ff_3_q, ~Enable);  // AND_Gate
  and and_6 (and_6_out, set_valeur_heures_compteur_1_output_bus_1[2], Enable);
  and and_7 (and_7_out, d_ff_4_q, ~Enable);  // AND_Gate
  and and_8 (and_8_out, set_valeur_heures_compteur_1_output_bus_1[3], Enable);
  and and_9 (and_9_out, d_ff_5_q, ~Enable);  // AND_Gate
  and and_10 (and_10_out, set_valeur_heures_compteur_1_output_bus_2[0], Enable);
  and and_11 (and_11_out, d_ff_6_q, ~Enable);  // AND_Gate
  and and_12 (and_12_out, set_valeur_heures_compteur_1_output_bus_2[1], Enable);
  and and_13 (and_13_out, d_ff_7_q, ~Enable);  // AND_Gate
  and and_14 (and_14_out, set_valeur_heures_compteur_1_output_bus_2[2], Enable);
  and and_15 (and_15_out, d_ff_8_q, ~Enable);  // AND_Gate
  and and_16 (and_16_out, set_valeur_heures_compteur_1_output_bus_2[3], Enable);
  or or_1 (Nbr[0], and_1_out, and_2_out);
  or or_2 (Nbr[1], and_3_out, and_4_out);
  or or_3 (Nbr[2], and_5_out, and_6_out);
  or or_4 (Nbr[3], and_7_out, and_8_out);
  or or_5 (Nbr[4], and_9_out, and_10_out);
  or or_6 (Nbr[5], and_11_out, and_12_out);
  or or_7 (Nbr[6], and_13_out, and_14_out);
  or or_8 (Nbr[7], and_15_out, and_16_out);
endmodule

module valeur_memory (
  input  [7:0] Valeur,
  input  Garde_memoire,
  input  Clock,
  input  Reset,
  output [7:0] Output_bus_1
);

  Register register_1 (.D(Valeur), .en(Garde_memoire), .clk(Clock), .Q(Output_bus_1), .clr(Reset));
endmodule

module chanel_c_set (
  input  CH_C_set_mode,
  input  [1:0] Encodeur,
  input  Reset,
  input  Clock,
  input  Reset_general,
  output Set_alarme,
  output Set_chrono,
  output Set_decompteur,
  output Set_song,
  output Set_jeu,
  output Affichage_menu_0,
  output Affichage_menu_1,
  output Affichage_menu_2,
  output Affichage_menu_3
);

  wire compteur_set_1_y0, compteur_set_1_y1, compteur_set_1_y2;

  compteur_set compteur_set_1 (
    .Encodeur(Encodeur), .Reset(Reset), .Set_mode(CH_C_set_mode), .Clock(Clock),
    .Reset_general(Reset_general), .Y0(compteur_set_1_y0), .Y1(compteur_set_1_y1), .Y2(compteur_set_1_y2),
    .A1(Affichage_menu_0), .A2(Affichage_menu_1), .A3(Affichage_menu_2), .A4(Affichage_menu_3));
  and and_1 (Set_alarme, ~compteur_set_1_y0, ~compteur_set_1_y1, ~compteur_set_1_y2);  // AND_Gate
  and and_2 (Set_chrono, compteur_set_1_y0, ~compteur_set_1_y1, ~compteur_set_1_y2);  // AND_Gate
  and and_3 (Set_decompteur, ~compteur_set_1_y0, compteur_set_1_y1, ~compteur_set_1_y2);  // AND_Gate
  and and_4 (Set_song, compteur_set_1_y0, compteur_set_1_y1, ~compteur_set_1_y2);  // AND_Gate
  and and_5 (Set_jeu, ~compteur_set_1_y0, ~compteur_set_1_y1, compteur_set_1_y2);  // AND_Gate
endmodule

module compteur_chanel_c (
  input  CH_C,
  input  Clock,
  input  Chrono_selected,
  input  Reset_input,
  output Mode_menu,
  output Ajuster_sec,
  output Ajuster_min,
  output Ajuster_heures,
  output Fonction_enable,
  output Reset
);

  wire d_ff_1_q, or_1_out;
  wire [2:0] counter_1_q, counter_2_q;

  or or_1 (or_1_out, Reset_input, Chrono_selected, Reset);
  D_Flip_Flop d_ff_1 (.D(Reset), .clk(Clock), .Q(d_ff_1_q), .preset(1'b0), .reset(Reset_input));  // open: Qn
  Counter #(.max('h5), .width(3)) counter_1 (
    .clr(or_1_out), .load(Chrono_selected), .up(1'b1), .count(CH_C), .clk(Clock), .D(3'b101), .Q(counter_1_q));  // open: carry
  Counter #(.max('h7), .width(3)) counter_2 (
    .clr(Reset_input), .load(d_ff_1_q), .up(1'b1), .count(CH_C), .clk(Clock), .D(3'b000), .Q(counter_2_q));  // open: carry
  and and_1 (Reset, counter_2_q[0], counter_2_q[1], counter_2_q[2]);
  and and_2 (Mode_menu, counter_1_q[0], ~counter_1_q[1], ~counter_1_q[2]);  // AND_Gate
  and and_3 (Ajuster_sec, ~counter_1_q[0], counter_1_q[1], ~counter_1_q[2]);  // AND_Gate
  and and_4 (Ajuster_min, counter_1_q[0], counter_1_q[1], ~counter_1_q[2]);  // AND_Gate
  and and_5 (Ajuster_heures, ~counter_1_q[0], ~counter_1_q[1], counter_1_q[2]);  // AND_Gate
  and and_6 (Fonction_enable, counter_1_q[0], ~counter_1_q[1], counter_1_q[2]);  // AND_Gate

  // Other names for the same wires on the sheet: channel_c = CH_C

  // Notes on the sheet:
  //   M3 increment counter
  //   M4 to decrement
  //   M2 switch to allow counting
endmodule
module compteur_59 (
  input  CH_A,
  input  CH_B,
  input  Reset_general,
  input  Enable,
  input  Clock,
  input  Reset_synchrone,
  output [3:0] Output_bus_1,
  output [3:0] Output_bus_2
);

  wire and_1_out, and_2_out, and_3_out, and_4_out, and_5_out, and_6_out, and_7_out, and_8_out, and_10_out,
       and_11_out, count, counter_output, d_ff_1_q, d_ff_2_q, d_ff_3_q, d_ff_4_q, d_ff_5_q, d_ff_6_q,
       d_ff_8_q, d_ff_9_q, d_ff_10_q, d_ff_11_q, d_ff_12_q, d_ff_13_q, d_ff_14_q, d_ff_15_q, load,
       multiplexer_1_out, multiplexer_2_out, nand_1_out, nand_2_out, nand_3_out, nand_4_out, nor_1_out,
       nor_2_out, not_1_out, not_2_out, or_1_out, or_2_out, or_3_out, or_4_out, or_5_out, or_6_out, or_7_out,
       or_8_out;
  wire [1:0] counter_1_q;
  wire [7:0] counter_2_q;

  and and_1 (and_1_out, load, Enable);
  D_Flip_Flop d_ff_1 (.D(CH_A), .clk(Clock), .Q(d_ff_1_q), .preset(1'b0), .reset(Reset_general));  // open: Qn
  D_Flip_Flop d_ff_2 (.D(CH_B), .clk(Clock), .Q(d_ff_2_q), .preset(1'b0), .reset(Reset_general));  // open: Qn
  D_Flip_Flop d_ff_3 (.D(d_ff_1_q), .clk(Clock), .Q(d_ff_3_q), .preset(1'b0), .reset(Reset_general));  // open: Qn
  D_Flip_Flop d_ff_4 (.D(d_ff_2_q), .clk(Clock), .Q(d_ff_4_q), .preset(1'b0), .reset(Reset_general));  // open: Qn
  and and_2 (and_2_out, counter_output, Enable);
  D_Flip_Flop d_ff_5 (.D(d_ff_3_q), .clk(Clock), .Q(d_ff_5_q), .preset(1'b0), .reset(Reset_general));  // open: Qn
  D_Flip_Flop d_ff_6 (.D(d_ff_4_q), .clk(Clock), .Q(d_ff_6_q), .preset(1'b0), .reset(Reset_general));  // open: Qn
  Counter #(.max('h1), .width(2)) counter_1 (
    .clr(Reset_general), .load(1'b0), .up(1'b1), .count(count), .clk(Clock), .D(2'b00), .Q(counter_1_q));  // open: carry
  Counter #(.max('h3b)) counter_2 (
    .clr(Reset_general), .load(Reset_synchrone), .up(and_1_out), .count(and_2_out), .clk(Clock),
    .D({8{1'b0}}), .Q(counter_2_q));  // open: carry
  and and_3 (and_3_out, d_ff_1_q, d_ff_5_q, d_ff_3_q);
  nor nor_1 (nor_1_out, d_ff_5_q, d_ff_1_q, d_ff_3_q);
  and and_4 (and_4_out, d_ff_2_q, d_ff_4_q, d_ff_6_q);
  nor nor_2 (nor_2_out, d_ff_6_q, d_ff_4_q, d_ff_2_q);
  D_Flip_Flop d_ff_7 (
    .D(and_5_out), .clk(Clock), .Q(counter_output), .preset(1'b0), .reset(Reset_general));  // open: Qn
  and and_5 (and_5_out, counter_1_q[0], d_ff_8_q);
  or or_1 (or_1_out, and_3_out, nor_1_out);
  or or_2 (or_2_out, and_4_out, nor_2_out);
  and and_6 (and_6_out, ~counter_1_q[0], ~counter_1_q[1]);  // AND_Gate
  // Binary_to_BCD_converter #(.binvalue(8)) binary_to_bcd_converter_1: pin names not known; wires that end beside it: counter_2_q, Output_bus_2, Output_bus_1
  Multiplexer multiplexer_1 (.in0(d_ff_9_q), .in1(d_ff_5_q), .out(multiplexer_1_out), .sel(or_1_out));
  Multiplexer multiplexer_2 (.in0(d_ff_10_q), .in1(d_ff_6_q), .out(multiplexer_2_out), .sel(or_2_out));
  D_Flip_Flop d_ff_8 (.D(and_6_out), .clk(Clock), .Q(d_ff_8_q), .preset(1'b0), .reset(Reset_general));  // open: Qn
  D_Flip_Flop d_ff_9 (
    .D(multiplexer_1_out), .clk(Clock), .Q(d_ff_9_q), .preset(1'b0), .reset(Reset_general));  // open: Qn
  D_Flip_Flop d_ff_10 (
    .D(multiplexer_2_out), .clk(Clock), .Q(d_ff_10_q), .preset(1'b0), .reset(Reset_general));  // open: Qn
  D_Flip_Flop d_ff_11 (.D(d_ff_9_q), .clk(Clock), .Q(d_ff_11_q), .preset(1'b0), .reset(Reset_general));  // open: Qn
  D_Flip_Flop d_ff_12 (.D(d_ff_10_q), .clk(Clock), .Q(d_ff_12_q), .preset(1'b0), .reset(Reset_general));  // open: Qn
  or or_3 (or_3_out, d_ff_9_q, d_ff_11_q);
  nand nand_1 (nand_1_out, d_ff_9_q, d_ff_11_q);
  or or_4 (or_4_out, d_ff_10_q, d_ff_12_q);
  nand nand_2 (nand_2_out, d_ff_10_q, d_ff_12_q);
  and and_7 (and_7_out, or_3_out, nand_1_out);
  and and_8 (and_8_out, or_4_out, nand_2_out);
  or or_5 (or_5_out, and_7_out, and_8_out);
  not not_1 (not_1_out, d_ff_9_q);
  not not_2 (not_2_out, d_ff_12_q);
  D_Flip_Flop d_ff_13 (.D(or_5_out), .clk(Clock), .Q(d_ff_13_q), .preset(1'b0), .reset(Reset_general));  // open: Qn
  or or_6 (or_6_out, d_ff_10_q, d_ff_11_q);
  or or_7 (or_7_out, d_ff_12_q, not_1_out);
  or or_8 (or_8_out, d_ff_9_q, not_2_out);
  nand nand_3 (nand_3_out, d_ff_10_q, d_ff_11_q);
  and and_9 (count, or_5_out, ~d_ff_13_q);  // AND_Gate
  nand nand_4 (nand_4_out, or_6_out, or_7_out, or_8_out, nand_3_out);
  and and_10 (and_10_out, count, nand_4_out);
  D_Flip_Flop d_ff_14 (.D(and_10_out), .clk(Clock), .Q(d_ff_14_q), .preset(1'b0), .reset(Reset_general));  // open: Qn
  and and_11 (and_11_out, and_10_out, ~d_ff_14_q);  // AND_Gate
  D_Flip_Flop d_ff_15 (.D(and_11_out), .clk(Clock), .Q(d_ff_15_q), .preset(1'b0), .reset(Reset_general));  // open: Qn
  D_Flip_Flop d_ff_16 (.D(d_ff_15_q), .clk(Clock), .Q(load), .preset(1'b0), .reset(Reset_general));  // open: Qn

  // Other names for the same wires on the sheet: reset = Reset_general

  // Notes on the sheet:
  //   B
  //   M3 increment counter
  //   M4 to decrement
  //   M2 switch to allow counting
  //   y1
  //   y2
  //   x1
  //   x2
  //   change signal
  //   count
  //   load
endmodule

module set_valeur_heures_compteur (
  input  [1:0] Decodeur,
  input  Reset_general,
  input  Enable,
  input  Clock,
  input  Reset_synchrone,
  output [3:0] Output_bus_1,
  output [3:0] Output_bus_2
);

  wire and_1_out, and_2_out, and_3_out, and_4_out, and_5_out, and_6_out, and_7_out, and_8_out, and_10_out,
       and_11_out, count_output, counter_output, d_ff_2_q, d_ff_3_q, d_ff_4_q, d_ff_5_q, d_ff_6_q, d_ff_7_q,
       d_ff_8_q, d_ff_9_q, d_ff_10_q, d_ff_11_q, d_ff_12_q, d_ff_13_q, d_ff_14_q, d_ff_15_q, load_output,
       multiplexer_1_out, multiplexer_2_out, nand_1_out, nand_2_out, nand_3_out, nand_4_out, nor_1_out,
       nor_2_out, not_1_out, not_2_out, or_1_out, or_2_out, or_3_out, or_4_out, or_5_out, or_6_out, or_7_out,
       or_8_out;
  wire [1:0] counter_1_q;
  wire [7:0] counter_2_q;

  and and_1 (and_1_out, load_output, Enable);
  and and_2 (and_2_out, counter_output, Enable);
  Counter #(.max('h1), .width(2)) counter_1 (
    .clr(Reset_general), .load(1'b0), .up(1'b1), .count(count_output), .clk(Clock), .D(2'b00), .Q(counter_1_q));  // open: carry
  Counter #(.max('h17)) counter_2 (
    .clr(Reset_general), .load(Reset_synchrone), .up(and_1_out), .count(and_2_out), .clk(Clock),
    .D({8{1'b0}}), .Q(counter_2_q));  // open: carry
  D_Flip_Flop d_ff_1 (
    .D(and_3_out), .clk(Clock), .Q(counter_output), .preset(1'b0), .reset(Reset_general));  // open: Qn
  and and_3 (and_3_out, counter_1_q[0], d_ff_2_q);
  and and_4 (and_4_out, ~counter_1_q[0], ~counter_1_q[1]);  // AND_Gate
  // Binary_to_BCD_converter #(.binvalue(8)) binary_to_bcd_converter_1: pin names not known; wires that end beside it: counter_2_q, Output_bus_2, Output_bus_1
  D_Flip_Flop d_ff_2 (.D(and_4_out), .clk(Clock), .Q(d_ff_2_q), .preset(1'b0), .reset(Reset_general));  // open: Qn
  D_Flip_Flop d_ff_3 (.D(Decodeur[0]), .clk(Clock), .Q(d_ff_3_q), .preset(1'b0), .reset(Reset_general));  // open: Qn
  D_Flip_Flop d_ff_4 (.D(Decodeur[1]), .clk(Clock), .Q(d_ff_4_q), .preset(1'b0), .reset(Reset_general));  // open: Qn
  D_Flip_Flop d_ff_5 (.D(d_ff_4_q), .clk(Clock), .Q(d_ff_5_q), .preset(1'b0), .reset(Reset_general));  // open: Qn
  D_Flip_Flop d_ff_6 (.D(d_ff_3_q), .clk(Clock), .Q(d_ff_6_q), .preset(1'b0), .reset(Reset_general));  // open: Qn
  D_Flip_Flop d_ff_7 (.D(d_ff_5_q), .clk(Clock), .Q(d_ff_7_q), .preset(1'b0), .reset(Reset_general));  // open: Qn
  D_Flip_Flop d_ff_8 (.D(d_ff_6_q), .clk(Clock), .Q(d_ff_8_q), .preset(1'b0), .reset(Reset_general));  // open: Qn
  and and_5 (and_5_out, d_ff_3_q, d_ff_8_q, d_ff_6_q);
  nor nor_1 (nor_1_out, d_ff_8_q, d_ff_3_q, d_ff_6_q);
  and and_6 (and_6_out, d_ff_4_q, d_ff_5_q, d_ff_7_q);
  nor nor_2 (nor_2_out, d_ff_7_q, d_ff_5_q, d_ff_4_q);
  or or_1 (or_1_out, and_5_out, nor_1_out);
  or or_2 (or_2_out, and_6_out, nor_2_out);
  Multiplexer multiplexer_1 (.in0(d_ff_9_q), .in1(d_ff_8_q), .out(multiplexer_1_out), .sel(or_1_out));
  Multiplexer multiplexer_2 (.in0(d_ff_10_q), .in1(d_ff_7_q), .out(multiplexer_2_out), .sel(or_2_out));
  D_Flip_Flop d_ff_9 (
    .D(multiplexer_1_out), .clk(Clock), .Q(d_ff_9_q), .preset(1'b0), .reset(Reset_general));  // open: Qn
  D_Flip_Flop d_ff_10 (
    .D(multiplexer_2_out), .clk(Clock), .Q(d_ff_10_q), .preset(1'b0), .reset(Reset_general));  // open: Qn
  D_Flip_Flop d_ff_11 (.D(d_ff_9_q), .clk(Clock), .Q(d_ff_11_q), .preset(1'b0), .reset(Reset_general));  // open: Qn
  D_Flip_Flop d_ff_12 (.D(d_ff_10_q), .clk(Clock), .Q(d_ff_12_q), .preset(1'b0), .reset(Reset_general));  // open: Qn
  or or_3 (or_3_out, d_ff_9_q, d_ff_11_q);
  nand nand_1 (nand_1_out, d_ff_9_q, d_ff_11_q);
  or or_4 (or_4_out, d_ff_10_q, d_ff_12_q);
  nand nand_2 (nand_2_out, d_ff_10_q, d_ff_12_q);
  and and_7 (and_7_out, or_3_out, nand_1_out);
  and and_8 (and_8_out, or_4_out, nand_2_out);
  or or_5 (or_5_out, and_7_out, and_8_out);
  or or_6 (or_6_out, d_ff_10_q, d_ff_11_q);
  or or_7 (or_7_out, d_ff_12_q, not_1_out);
  not not_1 (not_1_out, d_ff_9_q);
  or or_8 (or_8_out, d_ff_9_q, not_2_out);
  not not_2 (not_2_out, d_ff_12_q);
  D_Flip_Flop d_ff_13 (.D(or_5_out), .clk(Clock), .Q(d_ff_13_q), .preset(1'b0), .reset(Reset_general));  // open: Qn
  nand nand_3 (nand_3_out, d_ff_10_q, d_ff_11_q);
  and and_9 (count_output, or_5_out, ~d_ff_13_q);  // AND_Gate
  nand nand_4 (nand_4_out, or_6_out, or_7_out, or_8_out, nand_3_out);
  and and_10 (and_10_out, count_output, nand_4_out);
  D_Flip_Flop d_ff_14 (.D(and_10_out), .clk(Clock), .Q(d_ff_14_q), .preset(1'b0), .reset(Reset_general));  // open: Qn
  and and_11 (and_11_out, and_10_out, ~d_ff_14_q);  // AND_Gate
  D_Flip_Flop d_ff_15 (.D(and_11_out), .clk(Clock), .Q(d_ff_15_q), .preset(1'b0), .reset(Reset_general));  // open: Qn
  D_Flip_Flop d_ff_16 (.D(d_ff_15_q), .clk(Clock), .Q(load_output), .preset(1'b0), .reset(Reset_general));  // open: Qn

  // Other names for the same wires on the sheet: reset = Reset_general

  // Notes on the sheet:
  //   M4 to decrement
  //   M2 switch to allow counting
  //   M3 increment counter
  //   B
  //   y1
  //   y2
  //   x1
  //   x2
  //   change signal
  //   count
  //   load
endmodule

module decompteur (
  input  Clock,
  input  [7:0] Secondes,
  input  [7:0] Minutes,
  input  [7:0] Heures,
  input  Fonction_enable,
  input  Stop_alarme,
  input  load,
  input  Reset,
  input  Clock_bouton,
  output [7:0] Secondes_out,
  output [7:0] Minutes_out,
  output [7:0] Heures_out,
  output Buzzer
);

  wire and_1_out, and_2_out, and_3_out, and_4_out, and_5_out, and_6_out, and_7_out, and_8_out, and_9_out,
       and_10_out, and_11_out, and_12_out, and_13_out, and_14_out, and_15_out, comparator_1_eq,
       comparator_2_eq, comparator_3_eq, d_ff_1_q, not_1_out, not_2_out, not_3_out, or_1_out, or_2_out,
       or_3_out, or_4_out, or_5_out, or_6_out, or_7_out, or_8_out, register_1_q;
  wire [1:0] counter_7_q;

  or or_1 (or_1_out, not_1_out, and_1_out);
  or or_2 (or_2_out, not_1_out, and_2_out);
  or or_3 (or_3_out, not_1_out, and_3_out);
  or or_4 (or_4_out, not_1_out, and_4_out);
  or or_5 (or_5_out, not_1_out, and_5_out);
  not not_1 (not_1_out, load);
  and and_1 (and_1_out, and_13_out, Fonction_enable);
  and and_2 (and_2_out, and_6_out, Fonction_enable);
  and and_3 (and_3_out, and_7_out, Fonction_enable);
  and and_4 (and_4_out, and_8_out, Fonction_enable);
  and and_5 (and_5_out, and_9_out, Fonction_enable);
  or or_6 (or_6_out, register_1_q, Reset);
  Counter #(.max('h9), .width(4)) counter_1 (
    .clr(or_6_out), .load(not_1_out), .up(1'b0), .count(Fonction_enable), .clk(Clock), .D(Secondes[3:0]),
    .Q(Secondes_out[3:0]));  // open: carry
  Counter #(.max('h5), .width(4)) counter_2 (
    .clr(register_1_q), .load(not_1_out), .up(1'b0), .count(or_1_out), .clk(Clock), .D(Secondes[7:4]),
    .Q(Secondes_out[7:4]));  // open: carry
  Counter #(.max('h9), .width(4)) counter_3 (
    .clr(register_1_q), .load(not_1_out), .up(1'b0), .count(or_2_out), .clk(Clock), .D(Minutes[3:0]),
    .Q(Minutes_out[3:0]));  // open: carry
  Counter #(.max('h5), .width(4)) counter_4 (
    .clr(register_1_q), .load(not_1_out), .up(1'b0), .count(or_3_out), .clk(Clock), .D(Minutes[7:4]),
    .Q(Minutes_out[7:4]));  // open: carry
  Counter #(.max('h9), .width(4)) counter_5 (
    .clr(register_1_q), .load(not_1_out), .up(1'b0), .count(or_4_out), .clk(Clock), .D(Heures[3:0]),
    .Q(Heures_out[3:0]));  // open: carry
  Counter #(.max('h2), .width(4)) counter_6 (
    .clr(register_1_q), .load(not_1_out), .up(1'b0), .count(or_5_out), .clk(Clock), .D(Heures[7:4]),
    .Q(Heures_out[7:4]));  // open: carry
  Counter #(.max('h1), .width(2)) counter_7 (
    .clr(Reset), .load(not_1_out), .up(1'b0), .count(Stop_alarme), .clk(Clock_bouton), .D(2'b00),
    .Q(counter_7_q));  // open: carry
  and and_6 (and_6_out, and_13_out, and_10_out);
  and and_7 (and_7_out, and_6_out, and_11_out);
  and and_8 (and_8_out, and_7_out, and_12_out);
  and and_9 (and_9_out, and_8_out, and_14_out);
  and and_10 (and_10_out, ~Secondes_out[4], ~Secondes_out[5], ~Secondes_out[6], ~Secondes_out[7]);  // AND_Gate
  and and_11 (and_11_out, ~Minutes_out[0], ~Minutes_out[1], ~Minutes_out[2], ~Minutes_out[3]);  // AND_Gate
  and and_12 (and_12_out, ~Minutes_out[4], ~Minutes_out[5], ~Minutes_out[6], ~Minutes_out[7]);  // AND_Gate
  or or_7 (or_7_out, counter_7_q[0], counter_7_q[1]);
  and and_13 (and_13_out, ~Secondes_out[0], ~Secondes_out[1], ~Secondes_out[2], ~Secondes_out[3]);  // AND_Gate
  and and_14 (and_14_out, ~Heures_out[0], ~Heures_out[1], ~Heures_out[2], ~Heures_out[3]);  // AND_Gate
  not not_2 (not_2_out, register_1_q);
  Comparator comparator_1 (.a(Secondes_out), .b({8{1'b0}}), .eq(comparator_1_eq));  // open: gt, lt
  Comparator comparator_2 (.a(Minutes_out), .b({8{1'b0}}), .eq(comparator_2_eq));  // open: gt, lt
  Comparator comparator_3 (.a({8{1'b0}}), .b(Heures_out), .eq(comparator_3_eq));  // open: gt, lt
  not not_3 (not_3_out, Fonction_enable);
  and and_15 (and_15_out, comparator_1_eq, Fonction_enable, d_ff_1_q, comparator_2_eq, comparator_3_eq);
  Register #(.width(1)) register_1 (.D(and_15_out), .en(not_2_out), .clk(Clock), .Q(register_1_q), .clr(or_8_out));
  or or_8 (or_8_out, Reset, not_3_out);
  D_Flip_Flop d_ff_1 (.D(Secondes_out[0]), .clk(Clock), .Q(d_ff_1_q), .preset(1'b0), .reset(Reset));  // open: Qn
  and and_16 (Buzzer, register_1_q, ~or_7_out, Fonction_enable);  // AND_Gate
endmodule

module compteur_set (
  input  [1:0] Encodeur,
  input  Reset,
  input  Set_mode,
  input  Clock,
  input  Reset_general,
  output Y0,
  output Y1,
  output Y2,
  output A1,
  output A2,
  output A3,
  output A4
);

  wire and_1_out, and_2_out, and_3_out, and_6_out, and_7_out, and_8_out, and_9_out, and_11_out, and_12_out,
       count_output, counter_output, d_ff_2_q, d_ff_3_q, d_ff_4_q, d_ff_5_q, d_ff_6_q, d_ff_7_q, d_ff_8_q,
       d_ff_9_q, d_ff_10_q, d_ff_11_q, d_ff_12_q, d_ff_13_q, d_ff_14_q, d_ff_15_q, load_output,
       multiplexer_1_out, multiplexer_2_out, nand_1_out, nand_2_out, not_1_out, not_2_out, or_1_out,
       or_4_out, or_5_out, or_6_out, or_7_out, or_8_out, or_9_out, xor_1_out, xor_2_out;
  wire [1:0] counter_1_q;

  and and_1 (and_1_out, counter_output, Set_mode);
  Counter #(.max('h1), .width(2)) counter_1 (
    .clr(Reset_general), .load(1'b0), .up(1'b1), .count(count_output), .clk(Clock), .D(2'b00), .Q(counter_1_q));  // open: carry
  Counter #(.max('h4), .width(3)) counter_2 (
    .clr(Reset_general), .load(Reset), .up(load_output), .count(and_1_out), .clk(Clock), .D(3'b000),
    .Q({Y2, Y1, Y0}));  // open: carry
  or or_1 (or_1_out, Y0, Y1);
  D_Flip_Flop d_ff_1 (
    .D(and_2_out), .clk(Clock), .Q(counter_output), .preset(1'b0), .reset(Reset_general));  // open: Qn
  and and_2 (and_2_out, counter_1_q[0], d_ff_4_q);
  and and_3 (and_3_out, ~counter_1_q[0], ~counter_1_q[1]);  // AND_Gate
  or or_2 (A1, Y1, Y2);
  and and_4 (A2, ~Y1, ~Y2, ~Y0);  // AND_Gate
  and and_5 (A3, ~Y2, or_1_out);  // AND_Gate
  or or_3 (A4, Y2, ~Y1, ~Y0);  // OR_Gate
  D_Flip_Flop d_ff_2 (.D(Encodeur[0]), .clk(Clock), .Q(d_ff_2_q), .preset(1'b0), .reset(Reset_general));  // open: Qn
  D_Flip_Flop d_ff_3 (.D(Encodeur[1]), .clk(Clock), .Q(d_ff_3_q), .preset(1'b0), .reset(Reset_general));  // open: Qn
  D_Flip_Flop d_ff_4 (.D(and_3_out), .clk(Clock), .Q(d_ff_4_q), .preset(1'b0), .reset(Reset_general));  // open: Qn
  D_Flip_Flop d_ff_5 (.D(d_ff_3_q), .clk(Clock), .Q(d_ff_5_q), .preset(1'b0), .reset(Reset_general));  // open: Qn
  D_Flip_Flop d_ff_6 (.D(d_ff_2_q), .clk(Clock), .Q(d_ff_6_q), .preset(1'b0), .reset(Reset_general));  // open: Qn
  D_Flip_Flop d_ff_7 (.D(d_ff_5_q), .clk(Clock), .Q(d_ff_7_q), .preset(1'b0), .reset(Reset_general));  // open: Qn
  D_Flip_Flop d_ff_8 (.D(d_ff_6_q), .clk(Clock), .Q(d_ff_8_q), .preset(1'b0), .reset(Reset_general));  // open: Qn
  and and_6 (and_6_out, d_ff_2_q, d_ff_8_q, d_ff_6_q);
  and and_7 (and_7_out, ~d_ff_8_q, ~d_ff_2_q, ~d_ff_6_q);  // AND_Gate
  and and_8 (and_8_out, d_ff_3_q, d_ff_5_q, d_ff_7_q);
  and and_9 (and_9_out, ~d_ff_7_q, ~d_ff_5_q, ~d_ff_3_q);  // AND_Gate
  or or_4 (or_4_out, and_6_out, and_7_out);
  or or_5 (or_5_out, and_8_out, and_9_out);
  Multiplexer multiplexer_1 (.in0(d_ff_9_q), .in1(d_ff_8_q), .out(multiplexer_1_out), .sel(or_4_out));
  Multiplexer multiplexer_2 (.in0(d_ff_10_q), .in1(d_ff_7_q), .out(multiplexer_2_out), .sel(or_5_out));
  D_Flip_Flop d_ff_9 (
    .D(multiplexer_1_out), .clk(Clock), .Q(d_ff_9_q), .preset(1'b0), .reset(Reset_general));  // open: Qn
  D_Flip_Flop d_ff_10 (
    .D(multiplexer_2_out), .clk(Clock), .Q(d_ff_10_q), .preset(1'b0), .reset(Reset_general));  // open: Qn
  D_Flip_Flop d_ff_11 (.D(d_ff_9_q), .clk(Clock), .Q(d_ff_11_q), .preset(1'b0), .reset(Reset_general));  // open: Qn
  D_Flip_Flop d_ff_12 (.D(d_ff_10_q), .clk(Clock), .Q(d_ff_12_q), .preset(1'b0), .reset(Reset_general));  // open: Qn
  xor xor_1 (xor_1_out, d_ff_9_q, d_ff_11_q);
  xor xor_2 (xor_2_out, d_ff_10_q, d_ff_12_q);
  or or_6 (or_6_out, xor_1_out, xor_2_out);
  or or_7 (or_7_out, d_ff_10_q, d_ff_11_q);
  or or_8 (or_8_out, d_ff_12_q, not_1_out);
  not not_1 (not_1_out, d_ff_9_q);
  or or_9 (or_9_out, d_ff_9_q, not_2_out);
  not not_2 (not_2_out, d_ff_12_q);
  D_Flip_Flop d_ff_13 (.D(or_6_out), .clk(Clock), .Q(d_ff_13_q), .preset(1'b0), .reset(Reset_general));  // open: Qn
  nand nand_1 (nand_1_out, d_ff_10_q, d_ff_11_q);
  and and_10 (count_output, or_6_out, ~d_ff_13_q);  // AND_Gate
  nand nand_2 (nand_2_out, or_7_out, or_8_out, or_9_out, nand_1_out);
  and and_11 (and_11_out, count_output, nand_2_out);
  D_Flip_Flop d_ff_14 (.D(and_11_out), .clk(Clock), .Q(d_ff_14_q), .preset(1'b0), .reset(Reset_general));  // open: Qn
  and and_12 (and_12_out, and_11_out, ~d_ff_14_q);  // AND_Gate
  D_Flip_Flop d_ff_15 (.D(and_12_out), .clk(Clock), .Q(d_ff_15_q), .preset(1'b0), .reset(Reset_general));  // open: Qn
  D_Flip_Flop d_ff_16 (.D(d_ff_15_q), .clk(Clock), .Q(load_output), .preset(1'b0), .reset(Reset_general));  // open: Qn

  // Other names for the same wires on the sheet: reset_asynchrone = Reset; reset_t = Reset_general

  // Notes on the sheet:
  //   A=11
  //   B2
  //   B1
  //   B0
  //   M4 to decrement
  //   M2 switch to allow counting
  //   M3 increment counter
  //   B
  //   y1
  //   y2
  //   x1
  //   x2
  //   change signal
  //   toujours à 1
  //   count
  //   load
endmodule

module letter (
  input  Y_0,
  input  Y_1,
  input  Y_2,
  input  Y_3,
  output a,
  output b,
  output c,
  output d,
  output e,
  output f,
  output g
);

  wire and_1_out, and_2_out, and_3_out, and_4_out, and_5_out, and_6_out, and_7_out, and_8_out, and_9_out,
       and_10_out, and_11_out, and_12_out, and_13_out, and_14_out, and_15_out, and_16_out, and_17_out,
       and_18_out, and_19_out, and_20_out, and_21_out, and_22_out, and_23_out, and_24_out, and_25_out,
       not_1_out, not_2_out, not_3_out, not_4_out;

  not not_1 (not_1_out, Y_0);
  not not_2 (not_2_out, Y_1);
  not not_3 (not_3_out, Y_2);
  not not_4 (not_4_out, Y_3);
  and and_1 (and_1_out, not_1_out, not_2_out, Y_2, not_4_out);
  and and_2 (and_2_out, not_1_out, Y_1, not_3_out, not_4_out);
  and and_3 (and_3_out, not_2_out, not_3_out, Y_3);
  and and_4 (and_4_out, not_1_out, Y_1, not_3_out, not_4_out);
  and and_5 (and_5_out, not_2_out, not_3_out, Y_3);
  and and_6 (and_6_out, not_1_out, Y_1, not_4_out);
  and and_7 (and_7_out, not_1_out, Y_1, Y_2);
  and and_8 (and_8_out, Y_0, not_2_out, not_4_out);
  and and_9 (and_9_out, not_1_out, Y_2);
  and and_10 (and_10_out, not_2_out, Y_2, not_4_out);
  and and_11 (and_11_out, not_1_out, Y_1, not_4_out);
  and and_12 (and_12_out, Y_0, not_2_out, not_3_out, Y_3);
  and and_13 (and_13_out, not_1_out, not_2_out, Y_3);
  and and_14 (and_14_out, not_1_out, Y_2);
  and and_15 (and_15_out, not_2_out, Y_2);
  and and_16 (and_16_out, not_1_out, Y_1, not_4_out);
  and and_17 (and_17_out, Y_0, not_2_out, not_4_out);
  and and_18 (and_18_out, not_1_out, not_2_out, Y_3);
  and and_19 (and_19_out, not_1_out, not_2_out, Y_2);
  and and_20 (and_20_out, not_1_out, Y_1, not_4_out);
  and and_21 (and_21_out, not_1_out, not_3_out, Y_3);
  and and_22 (and_22_out, not_1_out, Y_2, not_4_out);
  and and_23 (and_23_out, not_1_out, Y_1, Y_2);
  and and_24 (and_24_out, Y_0, not_2_out, not_3_out, not_4_out);
  and and_25 (and_25_out, Y_0, not_2_out, Y_2, Y_3);
  or or_1 (a, and_1_out, and_2_out);
  or or_2 (b, and_3_out, and_4_out);
  or or_3 (c, and_5_out, and_6_out, and_7_out, and_8_out);
  or or_4 (d, and_9_out, and_10_out, and_11_out, and_12_out);
  or or_5 (e, and_13_out, and_14_out, and_15_out, and_16_out, and_17_out);
  or or_6 (f, and_18_out, and_19_out, and_20_out);
  or or_7 (g, and_21_out, and_22_out, and_23_out, and_24_out, and_25_out);
endmodule

module letter_affichage (
  input  Y_0,
  input  Y_1,
  input  Y_2,
  input  Y_3,
  output a,
  output b,
  output c,
  output d,
  output e,
  output f,
  output g
);

  letter letter_1 (.Y_0(Y_0), .Y_1(Y_1), .Y_2(Y_2), .Y_3(Y_3), .a(a), .b(b), .c(c), .d(d), .e(e), .f(f), .g(g));
endmodule

module letter_affichage_2 (
  input  Y_0,
  input  Y_1,
  input  Y_2,
  input  Y_3,
  output a,
  output b,
  output c,
  output d,
  output e,
  output f,
  output g
);

  wire and_2_out, and_3_out, and_4_out, and_5_out, and_6_out, and_7_out, and_8_out, and_9_out, and_10_out,
       and_11_out, and_12_out, and_13_out, and_14_out, and_15_out, and_16_out, and_17_out, and_18_out,
       and_19_out, and_20_out, and_21_out, and_22_out, not_1_out, not_2_out, not_3_out, not_4_out;

  not not_1 (not_1_out, Y_0);
  not not_2 (not_2_out, Y_1);
  not not_3 (not_3_out, Y_2);
  not not_4 (not_4_out, Y_3);
  and and_1 (a, not_1_out, Y_2);
  and and_2 (and_2_out, not_1_out, not_2_out, Y_3);
  and and_3 (and_3_out, not_1_out, not_2_out, Y_2);
  and and_4 (and_4_out, not_2_out, not_3_out, Y_3);
  and and_5 (and_5_out, not_2_out, Y_2, not_4_out);
  and and_6 (and_6_out, not_1_out, Y_1, Y_3);
  and and_7 (and_7_out, Y_0, not_2_out, Y_2);
  and and_8 (and_8_out, Y_0, Y_1, not_3_out, not_4_out);
  and and_9 (and_9_out, not_1_out, Y_1, Y_2);
  and and_10 (and_10_out, Y_0, not_2_out, not_3_out, Y_3);
  and and_11 (and_11_out, Y_0, not_2_out, Y_2, not_4_out);
  and and_12 (and_12_out, Y_0, Y_1, not_3_out, not_4_out);
  and and_13 (and_13_out, not_2_out, Y_3);
  and and_14 (and_14_out, not_2_out, Y_2);
  and and_15 (and_15_out, not_1_out, Y_1, not_4_out);
  and and_16 (and_16_out, Y_1, not_3_out);
  and and_17 (and_17_out, not_2_out, Y_3);
  and and_18 (and_18_out, not_1_out, Y_2);
  and and_19 (and_19_out, not_1_out, Y_1, not_4_out);
  and and_20 (and_20_out, not_3_out, Y_3);
  and and_21 (and_21_out, not_1_out, Y_2);
  and and_22 (and_22_out, Y_0, not_2_out);
  or or_1 (b, and_2_out, and_3_out);
  or or_2 (c, and_4_out, and_5_out, and_6_out, and_7_out, and_8_out);
  or or_3 (d, and_9_out, and_10_out, and_11_out, and_12_out);
  or or_4 (e, and_13_out, and_14_out, and_15_out, and_16_out);
  or or_5 (f, and_17_out, and_18_out, and_19_out);
  or or_6 (g, and_20_out, and_21_out, and_22_out);
endmodule

module controle (
  input  E,
  input  Y0,
  input  Y1,
  input  Y2,
  input  Y3,
  output Y0_output,
  output Y1_output,
  output Y2_output,
  output Y3_output,
  output E_output
);

  wire and_1_out, and_2_out, and_3_out, and_4_out, and_5_out, and_6_out, and_7_out, and_8_out, and_9_out,
       and_10_out, and_11_out, and_12_out, and_13_out, and_14_out, and_15_out, and_16_out, and_17_out,
       and_18_out, and_19_out, and_20_out, and_21_out, not_1_out, not_2_out, not_3_out, not_4_out, not_5_out;

  not not_1 (not_1_out, E);
  not not_2 (not_2_out, Y0);
  not not_3 (not_3_out, Y1);
  not not_4 (not_4_out, Y2);
  not not_5 (not_5_out, Y3);
  and and_1 (and_1_out, not_2_out, Y1, Y2, Y3);
  and and_2 (and_2_out, not_1_out, Y0, not_3_out, Y2, not_5_out);
  and and_3 (and_3_out, E, Y0, not_3_out, not_4_out, not_5_out);
  and and_4 (and_4_out, E, not_2_out, not_3_out, Y2, Y3);
  and and_5 (and_5_out, E, not_2_out, Y1, not_4_out);
  and and_6 (and_6_out, E, not_2_out, Y1, not_5_out);
  and and_7 (and_7_out, E, Y0, not_3_out, not_4_out, Y3);
  and and_8 (and_8_out, not_1_out, not_2_out, not_3_out, Y3);
  and and_9 (and_9_out, not_1_out, not_3_out, Y2, not_5_out);
  and and_10 (and_10_out, not_1_out, not_2_out, Y2, Y3);
  and and_11 (and_11_out, E, not_2_out, Y1, not_4_out, Y3);
  and and_12 (and_12_out, E, not_2_out, Y1, Y2, not_5_out);
  and and_13 (and_13_out, E, Y0, not_3_out, not_4_out, Y3);
  and and_14 (and_14_out, not_1_out, not_2_out, not_3_out, not_5_out);
  and and_15 (and_15_out, not_1_out, not_2_out, not_3_out, Y2);
  and and_16 (and_16_out, not_1_out, not_3_out, Y2, not_5_out);
  and and_17 (and_17_out, E, not_2_out, Y1, not_5_out);
  and and_18 (and_18_out, E, Y0, not_3_out, not_4_out);
  and and_19 (and_19_out, not_2_out, not_3_out, Y2, Y3);
  and and_20 (and_20_out, Y0, E, not_3_out, not_5_out, not_4_out);
  and and_21 (and_21_out, E, not_2_out, Y1);
  or or_1 (Y0_output, and_1_out, and_2_out, and_3_out);
  or or_2 (Y1_output, and_4_out, and_5_out, and_6_out, and_7_out);
  or or_3 (Y2_output, and_8_out, and_9_out, and_10_out, and_11_out, and_12_out, and_13_out);
  or or_4 (Y3_output, and_14_out, and_15_out, and_16_out, and_17_out, and_18_out);
  or or_5 (E_output, and_19_out, and_20_out, and_21_out);
endmodule

module controle_2 (
  input  Enable,
  input  Y_0,
  input  Y_1,
  input  Y_2,
  input  Y_3,
  output Y_0_output,
  output Y_1_output,
  output Y_2_output,
  output Y_3_output,
  output Enable_output
);

  wire and_1_out, and_2_out, and_3_out, and_4_out, and_5_out, and_6_out, and_7_out, and_8_out, and_9_out,
       and_10_out, and_11_out, and_12_out, and_13_out, and_14_out, and_15_out, and_16_out, and_17_out,
       and_18_out, and_19_out, and_20_out, and_21_out, not_1_out, not_2_out, not_3_out, not_4_out, not_5_out;

  not not_1 (not_1_out, Enable);
  not not_2 (not_2_out, Y_0);
  not not_3 (not_3_out, Y_1);
  not not_4 (not_4_out, Y_2);
  not not_5 (not_5_out, Y_3);
  and and_1 (and_1_out, not_2_out, not_3_out, Y_2, Y_3);
  and and_2 (and_2_out, Enable, not_2_out, Y_1, not_4_out);
  and and_3 (and_3_out, Enable, not_2_out, Y_1, not_5_out);
  and and_4 (and_4_out, not_1_out, not_2_out, Y_1);
  and and_5 (and_5_out, not_1_out, Y_0, not_3_out, not_4_out);
  and and_6 (and_6_out, not_1_out, Y_0, not_4_out, not_5_out);
  and and_7 (and_7_out, not_2_out, Y_1, Y_2, not_5_out);
  and and_8 (and_8_out, not_1_out, Y_0, not_3_out, Y_2);
  and and_9 (and_9_out, not_1_out, Y_0, Y_1, not_4_out, not_5_out);
  and and_10 (and_10_out, Enable, not_2_out, Y_2, Y_3);
  and and_11 (and_11_out, Enable, not_2_out, Y_1);
  and and_12 (and_12_out, not_1_out, not_3_out, Y_3);
  and and_13 (and_13_out, not_1_out, not_2_out, not_3_out, Y_2);
  and and_14 (and_14_out, not_2_out, Y_1, not_4_out, Y_3);
  and and_15 (and_15_out, Enable, not_2_out, Y_1, Y_2);
  and and_16 (and_16_out, not_1_out, not_3_out, not_5_out);
  and and_17 (and_17_out, not_1_out, not_4_out, not_5_out);
  and and_18 (and_18_out, not_1_out, not_2_out, not_3_out, Y_2);
  and and_19 (and_19_out, not_1_out, not_2_out, Y_1, not_4_out);
  and and_20 (and_20_out, not_2_out, Y_1, not_4_out, not_5_out);
  and and_21 (and_21_out, Enable, not_2_out, Y_1, Y_2);
  or or_1 (Enable_output, and_1_out, and_2_out, and_3_out);
  or or_2 (Y_0_output, and_4_out, and_5_out, and_6_out);
  or or_3 (Y_1_output, and_7_out, and_8_out, and_9_out, and_10_out, and_11_out);
  or or_4 (Y_2_output, and_12_out, and_13_out, and_14_out, and_15_out);
  or or_5 (Y_3_output, and_16_out, and_17_out, and_18_out, and_19_out, and_20_out, and_21_out);
endmodule

module letter_controle (
  input  Clock,
  input  Enable,
  input  Clock_counter,
  input  Reset,
  input  Enable_general,
  output Y0_output,
  output Y1_output,
  output Y2_output,
  output Y3_output
);

  wire and_1_out, controle_1_e_output, d_ff_1_q, d_ff_2_q, d_ff_3_q, d_ff_4_q, d_ff_5_q, nor_1_out, not_1_out;
  wire [4:0] counter_1_q;

  not not_1 (not_1_out, Enable_general);
  and and_1 (and_1_out, nor_1_out, Enable);
  Counter #(.max('h1c), .width(5)) counter_1 (
    .clr(Reset), .load(not_1_out), .up(1'b1), .count(and_1_out), .clk(Clock_counter), .D({5{1'b0}}),
    .Q(counter_1_q));  // open: carry
  controle controle_1 (
    .E(d_ff_5_q), .Y0(d_ff_1_q), .Y1(d_ff_2_q), .Y2(d_ff_3_q), .Y3(d_ff_4_q), .Y0_output(Y0_output),
    .Y1_output(Y1_output), .Y2_output(Y2_output), .Y3_output(Y3_output), .E_output(controle_1_e_output));
  nor nor_1 (nor_1_out, counter_1_q[1], counter_1_q[2], counter_1_q[0], counter_1_q[3], counter_1_q[4]);
  D_Flip_Flop d_ff_1 (.D(Y0_output), .clk(Clock), .Q(d_ff_1_q), .preset(nor_1_out), .reset(1'b0));  // open: Qn
  D_Flip_Flop d_ff_2 (.D(Y1_output), .clk(Clock), .Q(d_ff_2_q), .preset(nor_1_out), .reset(1'b0));  // open: Qn
  D_Flip_Flop d_ff_3 (.D(Y2_output), .clk(Clock), .Q(d_ff_3_q), .preset(1'b0), .reset(nor_1_out));  // open: Qn
  D_Flip_Flop d_ff_4 (.D(Y3_output), .clk(Clock), .Q(d_ff_4_q), .preset(nor_1_out), .reset(1'b0));  // open: Qn
  D_Flip_Flop d_ff_5 (
    .D(controle_1_e_output), .clk(Clock), .Q(d_ff_5_q), .preset(1'b0), .reset(nor_1_out));  // open: Qn

  // Notes on the sheet:
  //   1c
endmodule

module letter_controle_2 (
  input  Clock,
  input  Enable,
  input  Clock_counter,
  input  Reset,
  input  Enable_general,
  output Y0_output,
  output Y1_output,
  output Y2_output,
  output Y3_output
);

  wire and_1_out, controle_2_1_enable_output, d_ff_1_q, d_ff_2_q, d_ff_3_q, d_ff_4_q, d_ff_5_q, nor_1_out,
       not_1_out;
  wire [4:0] counter_1_q;

  and and_1 (and_1_out, nor_1_out, Enable);
  Counter #(.max('h1c), .width(5)) counter_1 (
    .clr(Reset), .load(not_1_out), .up(1'b1), .count(and_1_out), .clk(Clock_counter), .D({5{1'b0}}),
    .Q(counter_1_q));  // open: carry
  not not_1 (not_1_out, Enable_general);
  controle_2 controle_2_1 (
    .Enable(d_ff_5_q), .Y_0(d_ff_1_q), .Y_1(d_ff_2_q), .Y_2(d_ff_3_q), .Y_3(d_ff_4_q),
    .Y_0_output(Y0_output), .Y_1_output(Y1_output), .Y_2_output(Y2_output), .Y_3_output(Y3_output),
    .Enable_output(controle_2_1_enable_output));
  nor nor_1 (nor_1_out, counter_1_q[1], counter_1_q[2], counter_1_q[0], counter_1_q[3], counter_1_q[4]);
  D_Flip_Flop d_ff_1 (.D(Y0_output), .clk(Clock), .Q(d_ff_1_q), .preset(nor_1_out), .reset(1'b0));  // open: Qn
  D_Flip_Flop d_ff_2 (.D(Y1_output), .clk(Clock), .Q(d_ff_2_q), .preset(nor_1_out), .reset(1'b0));  // open: Qn
  D_Flip_Flop d_ff_3 (.D(Y2_output), .clk(Clock), .Q(d_ff_3_q), .preset(1'b0), .reset(nor_1_out));  // open: Qn
  D_Flip_Flop d_ff_4 (.D(Y3_output), .clk(Clock), .Q(d_ff_4_q), .preset(nor_1_out), .reset(1'b0));  // open: Qn
  D_Flip_Flop d_ff_5 (
    .D(controle_2_1_enable_output), .clk(Clock), .Q(d_ff_5_q), .preset(1'b0), .reset(nor_1_out));  // open: Qn

  // Notes on the sheet:
  //   1c
endmodule

module compteur_jeu (
  input  Start,
  input  Clock,
  input  Reset,
  output Show
);

  wire and_1_out, or_1_out;
  wire [1:0] counter_1_q;
  wire [2:0] counter_2_q, counter_3_q;

  Counter #(.max('h1), .ongoal("stay"), .width(2)) counter_1 (
    .clr(Reset), .load(and_1_out), .up(1'b1), .count(Start), .clk(Clock), .D(2'b00), .Q(counter_1_q));  // open: carry
  Counter #(.max('h7), .width(3)) counter_2 (
    .clr(Reset), .load(and_1_out), .up(1'b1), .count(Start), .clk(Clock), .D(3'b000), .Q(counter_2_q));  // open: carry
  Counter #(.max('h7), .width(3)) counter_3 (
    .clr(Reset), .load(and_1_out), .up(1'b1), .count(or_1_out), .clk(Clock), .D(3'b000), .Q(counter_3_q));  // open: carry
  or or_1 (or_1_out, counter_1_q[0], counter_1_q[1]);
  or or_2 (Show, counter_2_q[0], counter_2_q[1], counter_2_q[2]);
  and and_1 (and_1_out, counter_3_q[0], counter_3_q[1], counter_3_q[2]);
endmodule

module score (
  input  Answer_0,
  input  Answer_1,
  input  Answer_2,
  input  Answer_3,
  input  Answer_4,
  input  Answer_5,
  input  Answer_6,
  input  Input_0,
  input  Input_1,
  input  Input_2,
  input  Input_3,
  input  Input_4,
  input  Input_5,
  input  Input_6,
  output Result
);

  wire xor_1_out, xor_2_out, xor_3_out, xor_4_out, xor_5_out, xor_6_out, xor_7_out;

  xor xor_1 (xor_1_out, Answer_0, Input_0);
  xor xor_2 (xor_2_out, Answer_1, Input_1);
  xor xor_3 (xor_3_out, Answer_2, Input_2);
  xor xor_4 (xor_4_out, Answer_3, Input_3);
  xor xor_5 (xor_5_out, Answer_4, Input_4);
  xor xor_6 (xor_6_out, Answer_5, Input_5);
  xor xor_7 (xor_7_out, Answer_6, Input_6);
  nor nor_1 (Result, xor_1_out, xor_2_out, xor_3_out, xor_4_out, xor_5_out, xor_6_out, xor_7_out);
endmodule

module succes (
  input  Enable,
  output s_a,
  output s_b,
  output s_c,
  output s_d,
  output s_e,
  output s_f,
  output s_g,
  output u_a,
  output u_b,
  output u_c,
  output u_d,
  output u_e,
  output u_f,
  output u_g,
  output c_a,
  output c_b,
  output c_c,
  output c_d,
  output c_e,
  output c_f,
  output c_g,
  output e_a,
  output e_b,
  output e_c,
  output e_d,
  output e_e,
  output e_f,
  output e_g
);

  s_lettre s_1 (.enable(Enable), .a(s_a), .b(s_b), .c(s_c), .d(s_d), .e(s_e), .f(s_f), .g(s_g));
  u_lettre u_1 (.enable(Enable), .a(u_a), .b(u_b), .c(u_c), .d(u_d), .e(u_e), .f(u_f), .g(u_g));
  c_lettre c_1 (.enable(Enable), .a(c_a), .b(c_b), .c(c_c), .d(c_d), .e(c_e), .f(c_f), .g(c_g));
  e_lettre e_1 (.enable(Enable), .a(e_a), .b(e_b), .c(e_c), .d(e_d), .e(e_e), .f(e_f), .g(e_g));
endmodule

module Y_0 (
  input  A0,
  input  B0,
  input  Carry,
  output Y0_output,
  output C0
);

  wire and_1_out, and_2_out, xor_1_out, xor_2_out;

  and and_1 (and_1_out, A0, B0);
  xor xor_1 (xor_1_out, A0, B0);
  xor xor_2 (xor_2_out, xor_1_out, Carry);
  and and_2 (and_2_out, xor_1_out, Carry);
  Multiplexer multiplexer_1 (.in0(xor_1_out), .in1(xor_2_out), .out(Y0_output), .sel(Carry));
  Multiplexer multiplexer_2 (.in0(and_1_out), .in1(and_2_out), .out(C0), .sel(Carry));
endmodule

module Y_i (
  input  A_i,
  input  B_i,
  input  C_i,
  output Y_i_output,
  output C_i_output
);

  wire and_1_out, and_2_out, and_3_out, and_4_out, not_1_out, not_2_out, or_1_out, xor_1_out;

  xor xor_1 (xor_1_out, A_i, B_i);
  not not_1 (not_1_out, C_i);
  or or_1 (or_1_out, B_i, A_i);
  not not_2 (not_2_out, xor_1_out);
  and and_1 (and_1_out, xor_1_out, not_1_out);
  and and_2 (and_2_out, B_i, A_i);
  and and_3 (and_3_out, C_i, or_1_out);
  and and_4 (and_4_out, C_i, not_2_out);
  or or_2 (Y_i_output, and_4_out, and_1_out);
  or or_3 (C_i_output, and_2_out, and_3_out);
endmodule

module a (
  input  W,
  input  X,
  input  Y,
  input  Z,
  output a_output
);

  wire and_1_out, and_2_out, and_3_out, and_4_out, and_5_out, and_6_out, and_7_out, and_8_out, not_1_out,
       not_2_out, not_3_out, not_4_out, or_1_out, or_2_out, or_3_out;

  not not_1 (not_1_out, W);
  not not_2 (not_2_out, X);
  not not_3 (not_3_out, Y);
  not not_4 (not_4_out, Z);
  and and_1 (and_1_out, not_1_out, not_3_out);
  and and_2 (and_2_out, X, not_4_out);
  and and_3 (and_3_out, not_2_out, Z);
  and and_4 (and_4_out, W, Z);
  and and_5 (and_5_out, X, not_3_out);
  and and_6 (and_6_out, Y, not_2_out);
  or or_1 (or_1_out, and_2_out, and_3_out);
  or or_2 (or_2_out, and_5_out, and_6_out);
  and and_7 (and_7_out, and_1_out, or_1_out);
  and and_8 (and_8_out, and_4_out, or_2_out);
  or or_3 (or_3_out, and_7_out, and_8_out);
  not not_5 (a_output, or_3_out);
endmodule

module b (
  input  W,
  input  X,
  input  Y,
  input  Z,
  output b_output
);

  wire and_1_out, and_2_out, and_3_out, and_4_out, and_5_out, and_6_out, and_7_out, not_1_out, not_2_out,
       not_3_out, not_4_out, or_1_out, or_2_out;

  not not_1 (not_1_out, W);
  not not_2 (not_2_out, X);
  not not_3 (not_3_out, Y);
  not not_4 (not_4_out, Z);
  and and_1 (and_1_out, W, not_3_out);
  and and_2 (and_2_out, Y, not_1_out);
  and and_3 (and_3_out, not_2_out, Z);
  and and_4 (and_4_out, not_4_out, not_3_out);
  or or_1 (or_1_out, and_1_out, and_2_out);
  and and_5 (and_5_out, not_2_out, not_4_out);
  and and_6 (and_6_out, or_1_out, Z);
  or or_2 (or_2_out, and_3_out, and_4_out);
  and and_7 (and_7_out, or_2_out, not_1_out);
  or or_3 (b_output, and_5_out, and_6_out, and_7_out);
endmodule

module c (
  input  W,
  input  X,
  input  Y,
  input  Z,
  output c_output
);

  wire and_1_out, and_2_out, and_3_out, not_1_out, not_2_out, not_3_out, or_1_out;

  not not_1 (not_1_out, Z);
  not not_2 (not_2_out, X);
  not not_3 (not_3_out, W);
  and and_1 (and_1_out, W, X, Y);
  and and_2 (and_2_out, W, X, not_1_out);
  and and_3 (and_3_out, not_1_out, not_2_out, not_3_out, Y);
  or or_1 (or_1_out, and_1_out, and_2_out, and_3_out);
  not not_4 (c_output, or_1_out);
endmodule

module d (
  input  W,
  input  X,
  input  Y,
  input  Z,
  output d_output
);

  wire and_1_out, and_2_out, and_3_out, and_4_out, and_5_out, and_6_out, not_1_out, not_2_out, not_3_out,
       not_4_out, or_1_out;

  not not_1 (not_1_out, W);
  not not_2 (not_2_out, X);
  not not_3 (not_3_out, Z);
  not not_4 (not_4_out, Y);
  and and_1 (and_1_out, W, not_4_out);
  and and_2 (and_2_out, X, not_3_out);
  and and_3 (and_3_out, not_2_out, Z);
  and and_4 (and_4_out, not_3_out, not_1_out, not_2_out);
  and and_5 (and_5_out, Z, not_4_out, X);
  or or_1 (or_1_out, and_2_out, and_3_out);
  and and_6 (and_6_out, Y, or_1_out);
  or or_2 (d_output, and_1_out, and_6_out, and_4_out, and_5_out);
endmodule

module e (
  input  W,
  input  X,
  input  Y,
  input  Z,
  output e_output
);

  wire and_1_out, and_2_out, and_3_out, and_4_out, not_1_out, not_2_out, not_3_out;

  not not_1 (not_1_out, X);
  not not_2 (not_2_out, Z);
  not not_3 (not_3_out, W);
  and and_1 (and_1_out, W, X);
  and and_2 (and_2_out, W, Y);
  and and_3 (and_3_out, not_1_out, not_2_out);
  and and_4 (and_4_out, not_3_out, Y, not_2_out);
  or or_1 (e_output, and_1_out, and_2_out, and_3_out, and_4_out);
endmodule

module f (
  input  W,
  input  X,
  input  Y,
  input  Z,
  output f_output
);

  wire and_1_out, and_2_out, and_3_out, and_4_out, not_1_out, not_2_out, not_3_out, or_1_out;

  not not_1 (not_1_out, W);
  not not_2 (not_2_out, X);
  not not_3 (not_3_out, Y);
  and and_1 (and_1_out, W, X, not_3_out, Z);
  and and_2 (and_2_out, not_1_out, not_2_out, Y);
  and and_3 (and_3_out, not_1_out, Y, Z);
  and and_4 (and_4_out, Z, not_1_out, not_2_out);
  or or_1 (or_1_out, and_1_out, and_2_out, and_3_out, and_4_out);
  not not_4 (f_output, or_1_out);
endmodule

module g (
  input  W,
  input  X,
  input  Y,
  input  Z,
  output g_output
);

  wire and_1_out, and_2_out, and_3_out, and_4_out, not_1_out, not_2_out, not_3_out, not_4_out, or_1_out,
       or_2_out;

  not not_1 (not_1_out, W);
  not not_2 (not_2_out, Y);
  not not_3 (not_3_out, X);
  and and_1 (and_1_out, not_3_out, not_1_out, not_2_out);
  and and_2 (and_2_out, Y, not_1_out, Z);
  and and_3 (and_3_out, not_2_out, W, not_4_out);
  not not_4 (not_4_out, Z);
  or or_1 (or_1_out, and_2_out, and_3_out);
  and and_4 (and_4_out, X, or_1_out);
  or or_2 (or_2_out, and_1_out, and_4_out);
  not not_5 (g_output, or_2_out);
endmodule

module s_lettre (
  input  enable,
  output a,
  output b,
  output c,
  output d,
  output e,
  output f,
  output g
);

  Multiplexer multiplexer_1 (.in0(1'b0), .in1(1'b1), .out(a), .sel(enable));
  Multiplexer multiplexer_2 (.in0(1'b0), .in1(1'b1), .out(c), .sel(enable));
  Multiplexer multiplexer_3 (.in0(1'b0), .in1(1'b1), .out(d), .sel(enable));
  Multiplexer multiplexer_4 (.in0(1'b0), .in1(1'b1), .out(f), .sel(enable));
  Multiplexer multiplexer_5 (.in0(1'b0), .in1(1'b1), .out(g), .sel(enable));

  assign b = 1'b0;
  assign e = 1'b0;
endmodule

module u_lettre (
  input  enable,
  output a,
  output b,
  output c,
  output d,
  output e,
  output f,
  output g
);

  Multiplexer multiplexer_1 (.in0(1'b0), .in1(1'b1), .out(b), .sel(enable));
  Multiplexer multiplexer_2 (.in0(1'b0), .in1(1'b1), .out(c), .sel(enable));
  Multiplexer multiplexer_3 (.in0(1'b0), .in1(1'b1), .out(d), .sel(enable));
  Multiplexer multiplexer_4 (.in0(1'b0), .in1(1'b1), .out(e), .sel(enable));
  Multiplexer multiplexer_5 (.in0(1'b0), .in1(1'b1), .out(f), .sel(enable));

  assign a = 1'b0;
  assign g = 1'b0;
endmodule

module c_lettre (
  input  enable,
  output a,
  output b,
  output c,
  output d,
  output e,
  output f,
  output g
);

  Multiplexer multiplexer_1 (.in0(1'b0), .in1(1'b1), .out(a), .sel(enable));
  Multiplexer multiplexer_2 (.in0(1'b0), .in1(1'b1), .out(d), .sel(enable));
  Multiplexer multiplexer_3 (.in0(1'b0), .in1(1'b1), .out(e), .sel(enable));
  Multiplexer multiplexer_4 (.in0(1'b0), .in1(1'b1), .out(f), .sel(enable));

  assign b = 1'b0;
  assign c = 1'b0;
  assign g = 1'b0;
endmodule

module e_lettre (
  input  enable,
  output a,
  output b,
  output c,
  output d,
  output e,
  output f,
  output g
);

  Multiplexer multiplexer_1 (.in0(1'b0), .in1(1'b1), .out(a), .sel(enable));
  Multiplexer multiplexer_2 (.in0(1'b0), .in1(1'b1), .out(d), .sel(enable));
  Multiplexer multiplexer_3 (.in0(1'b0), .in1(1'b1), .out(e), .sel(enable));
  Multiplexer multiplexer_4 (.in0(1'b0), .in1(1'b1), .out(f), .sel(enable));
  Multiplexer multiplexer_5 (.in0(1'b0), .in1(1'b1), .out(g), .sel(enable));

  assign b = 1'b0;
  assign c = 1'b0;
endmodule
